// Logisim project 2 乘法器.circ as structural Verilog: 7 circuits, main circuit MUL 4*4 Prev
module MUL_4_4_Prev (
  input  [3:0] \输入a ,
  input  [3:0] \输入b ,
  output [7:0] \输出 
);

  wire [3:0] and_1_out, and_5_out, and_9_out, and_13_out;
  wire [7:0] adder_1_out, adder_2_out, bit_extender_1_out, bit_extender_2_out, bit_extender_3_out,
       bit_extender_4_out, shifter_1_out, shifter_2_out, shifter_3_out;

  and and_1 (and_1_out[0], \输入a [0], \输入b [0]);
  and and_2 (and_1_out[1], \输入a [1], \输入b [0]);
  and and_3 (and_1_out[2], \输入a [2], \输入b [0]);
  and and_4 (and_1_out[3], \输入a [3], \输入b [0]);
  and and_5 (and_5_out[0], \输入a [0], \输入b [2]);
  and and_6 (and_5_out[1], \输入a [1], \输入b [2]);
  and and_7 (and_5_out[2], \输入a [2], \输入b [2]);
  and and_8 (and_5_out[3], \输入a [3], \输入b [2]);
  and and_9 (and_9_out[0], \输入a [0], \输入b [1]);
  and and_10 (and_9_out[1], \输入a [1], \输入b [1]);
  and and_11 (and_9_out[2], \输入a [2], \输入b [1]);
  and and_12 (and_9_out[3], \输入a [3], \输入b [1]);
  and and_13 (and_13_out[0], \输入a [0], \输入b [3]);
  and and_14 (and_13_out[1], \输入a [1], \输入b [3]);
  and and_15 (and_13_out[2], \输入a [2], \输入b [3]);
  and and_16 (and_13_out[3], \输入a [3], \输入b [3]);
  assign bit_extender_1_out = {{4{1'b0}}, and_1_out};  // Bit_Extender bit_extender_1
  assign bit_extender_2_out = {{4{1'b0}}, and_9_out};  // Bit_Extender bit_extender_2
  assign bit_extender_3_out = {{4{1'b0}}, and_5_out};  // Bit_Extender bit_extender_3
  assign bit_extender_4_out = {{4{1'b0}}, and_13_out};  // Bit_Extender bit_extender_4
  Shifter #(.width(8), .shift("ll")) shifter_1 (.in(bit_extender_2_out), .\dist (3'b001), .out(shifter_1_out));
  Shifter #(.width(8), .shift("ll")) shifter_2 (.in(bit_extender_3_out), .\dist (3'b010), .out(shifter_2_out));
  Shifter #(.width(8), .shift("ll")) shifter_3 (.in(bit_extender_4_out), .\dist (3'b011), .out(shifter_3_out));
  Adder #(.width(8)) adder_1 (.a(bit_extender_1_out), .b(shifter_1_out), .out(adder_1_out), .cin(1'b0));  // open: cout
  Adder #(.width(8)) adder_2 (.a(adder_1_out), .b(shifter_2_out), .out(adder_2_out), .cin(1'b0));  // open: cout
  Adder #(.width(8)) adder_3 (.a(adder_2_out), .b(shifter_3_out), .out(\输出 ), .cin(1'b0));  // open: cout
endmodule

module \四位乘法器测试电路  (
  input  [3:0] in_1,
  input  [3:0] in_2,
  input  [3:0] in_3,
  input  [3:0] in_4,
  output [7:0] out_5,
  output [7:0] out_6
);

  MUL_4_4_Prev mul_4_4_prev_1 (.\输入a (in_1), .\输入b (in_2), .\输出 (out_5));
  MUL_4_4 mul_4_4_1 (.a(in_3), .b(in_4), .out_3(out_6));

  // Notes on the sheet:
  //   没有使用二路选择器
  //   使用二路选择器
endmodule

module \_32X4乘法器测试电路  (
  input  [31:0] in_1,
  input  [3:0] in_2,
  output [31:0] out_3,
  output out_4
);

  // MUL_32_4 mul_32_4_1: pin names not known; wires that end beside it: in_1, in_2, out_3, out_4
endmodule

module \_32X32乘法器测试电路  (
  input  [31:0] in_1,
  input  [31:0] in_2,
  output [31:0] out_3,
  output out_4
);

  MUL_32_32 mul_32_32_1 (.in_1(in_1), .in_2(in_2), .out_3(out_3), .\溢出判断 (out_4));
endmodule

module MUL_4_4 (
  input  [3:0] a,
  input  [3:0] b,
  output [7:0] out_3
);

  wire [7:0] adder_1_out, adder_2_out, adder_3_out, bit_extender_1_out, multiplexer_1_out, multiplexer_2_out,
       multiplexer_3_out, shifter_1_out, shifter_2_out, shifter_3_out;

  assign bit_extender_1_out = {{4{1'b0}}, a};  // Bit_Extender bit_extender_1
  Multiplexer #(.select(1), .width(8), .disabled("Z"), .enable("false")) multiplexer_1 (
    .in0({8{1'b0}}), .in1(bit_extender_1_out), .out(multiplexer_1_out), .sel(b[0]));
  Shifter #(.width(8), .shift("ll")) shifter_1 (.in(bit_extender_1_out), .\dist (3'b001), .out(shifter_1_out));
  Adder #(.width(8)) adder_1 (.a(multiplexer_1_out), .b(shifter_1_out), .out(adder_1_out));  // open: cin, cout
  Shifter #(.width(8), .shift("ll")) shifter_2 (.in(shifter_1_out), .\dist (3'b001), .out(shifter_2_out));
  Multiplexer #(.select(1), .width(8), .disabled("Z"), .enable("false")) multiplexer_2 (
    .in0(multiplexer_1_out), .in1(adder_1_out), .out(multiplexer_2_out), .sel(b[1]));
  Adder #(.width(8)) adder_2 (.a(multiplexer_2_out), .b(shifter_2_out), .out(adder_2_out));  // open: cin, cout
  Shifter #(.width(8), .shift("ll")) shifter_3 (.in(shifter_2_out), .\dist (3'b001), .out(shifter_3_out));
  Multiplexer #(.select(1), .width(8), .disabled("Z"), .enable("false")) multiplexer_3 (
    .in0(multiplexer_2_out), .in1(adder_2_out), .out(multiplexer_3_out), .sel(b[2]));
  Adder #(.width(8)) adder_3 (.a(multiplexer_3_out), .b(shifter_3_out), .out(adder_3_out));  // open: cin, cout
  Multiplexer #(.select(1), .width(8), .disabled("Z"), .enable("false")) multiplexer_4 (
    .in0(multiplexer_3_out), .in1(adder_3_out), .out(out_3), .sel(b[3]));
endmodule

module MUL_32_4 (
  input  [31:0] a,
  input  [3:0] b,
  output [31:0] \输出 ,
  output \溢出判断 
);

  wire [3:0] bitselector_1_out;
  wire [7:0] mul_4_4_1_out_3;
  wire [31:0] adder_1_out, adder_2_out, adder_3_out, multiplexer_1_out, multiplexer_2_out, multiplexer_3_out,
       shifter_1_out, shifter_2_out, shifter_3_out;

  Multiplexer #(.select(1), .width(32), .disabled("Z"), .enable("false")) multiplexer_1 (
    .in0({32{1'b0}}), .in1(a), .out(multiplexer_1_out), .sel(b[0]));
  Shifter #(.width(32), .shift("ll")) shifter_1 (.in(a), .\dist (5'b00001), .out(shifter_1_out));
  MUL_4_4 mul_4_4_1 (.a(bitselector_1_out), .b(b), .out_3(mul_4_4_1_out_3));
  BitSelector #(.width(32), .group(4)) bitselector_1 (.in(a), .out(bitselector_1_out), .sel(3'b111));
  Adder #(.width(32)) adder_1 (.a(multiplexer_1_out), .b(shifter_1_out), .out(adder_1_out));  // open: cin, cout
  Shifter #(.width(32), .shift("ll")) shifter_2 (.in(shifter_1_out), .\dist (5'b00001), .out(shifter_2_out));
  or or_1 (\溢出判断 , mul_4_4_1_out_3[4], mul_4_4_1_out_3[5], mul_4_4_1_out_3[6], mul_4_4_1_out_3[7]);
  Multiplexer #(.select(1), .width(32), .disabled("Z"), .enable("false")) multiplexer_2 (
    .in0(multiplexer_1_out), .in1(adder_1_out), .out(multiplexer_2_out), .sel(b[1]));
  Adder #(.width(32)) adder_2 (.a(multiplexer_2_out), .b(shifter_2_out), .out(adder_2_out));  // open: cin, cout
  Shifter #(.width(32), .shift("ll")) shifter_3 (.in(shifter_2_out), .\dist (5'b00001), .out(shifter_3_out));
  Multiplexer #(.select(1), .width(32), .disabled("Z"), .enable("false")) multiplexer_3 (
    .in0(multiplexer_2_out), .in1(adder_2_out), .out(multiplexer_3_out), .sel(b[2]));
  Adder #(.width(32)) adder_3 (.a(multiplexer_3_out), .b(shifter_3_out), .out(adder_3_out));  // open: cin, cout
  Multiplexer #(.select(1), .width(32), .disabled("Z"), .enable("false")) multiplexer_4 (
    .in0(multiplexer_3_out), .in1(adder_3_out), .out(\输出 ), .sel(b[3]));
endmodule

module MUL_32_32 (
  input  [31:0] in_1,
  input  [31:0] in_2,
  output [31:0] out_3,
  output \溢出判断 
);

  wire \mul_32_4_1_溢出判断 , \mul_32_4_2_溢出判断 , \mul_32_4_3_溢出判断 , \mul_32_4_4_溢出判断 , \mul_32_4_5_溢出判断 ,
       \mul_32_4_6_溢出判断 , \mul_32_4_7_溢出判断 , \mul_32_4_8_溢出判断 ;
  wire [3:0] bitselector_1_out, bitselector_2_out, bitselector_3_out, bitselector_4_out, bitselector_5_out,
       bitselector_6_out, bitselector_7_out, bitselector_8_out;
  wire [31:0] adder_1_out, adder_2_out, adder_3_out, adder_4_out, adder_5_out, adder_6_out, \mul_32_4_1_输出 ,
       \mul_32_4_2_输出 , \mul_32_4_3_输出 , \mul_32_4_4_输出 , \mul_32_4_5_输出 , \mul_32_4_6_输出 , \mul_32_4_7_输出 ,
       \mul_32_4_8_输出 , shifter_1_out, shifter_2_out, shifter_3_out, shifter_4_out, shifter_5_out,
       shifter_6_out, shifter_7_out;

  BitSelector #(.width(32), .group(4)) bitselector_1 (.in(in_2), .out(bitselector_1_out), .sel(3'b000));
  BitSelector #(.width(32), .group(4)) bitselector_2 (.in(in_2), .out(bitselector_2_out), .sel(3'b001));
  BitSelector #(.width(32), .group(4)) bitselector_3 (.in(in_2), .out(bitselector_3_out), .sel(3'b010));
  BitSelector #(.width(32), .group(4)) bitselector_4 (.in(in_2), .out(bitselector_4_out), .sel(3'b011));
  BitSelector #(.width(32), .group(4)) bitselector_5 (.in(in_2), .out(bitselector_5_out), .sel(3'b100));
  BitSelector #(.width(32), .group(4)) bitselector_6 (.in(in_2), .out(bitselector_6_out), .sel(3'b101));
  BitSelector #(.width(32), .group(4)) bitselector_7 (.in(in_2), .out(bitselector_7_out), .sel(3'b110));
  BitSelector #(.width(32), .group(4)) bitselector_8 (.in(in_2), .out(bitselector_8_out), .sel(3'b111));
  MUL_32_4 mul_32_4_1 (.a(in_1), .b(bitselector_1_out), .\输出 (\mul_32_4_1_输出 ), .\溢出判断 (\mul_32_4_1_溢出判断 ));
  MUL_32_4 mul_32_4_2 (.a(in_1), .b(bitselector_2_out), .\输出 (\mul_32_4_2_输出 ), .\溢出判断 (\mul_32_4_2_溢出判断 ));
  MUL_32_4 mul_32_4_3 (.a(in_1), .b(bitselector_3_out), .\输出 (\mul_32_4_3_输出 ), .\溢出判断 (\mul_32_4_3_溢出判断 ));
  MUL_32_4 mul_32_4_4 (.a(in_1), .b(bitselector_4_out), .\输出 (\mul_32_4_4_输出 ), .\溢出判断 (\mul_32_4_4_溢出判断 ));
  MUL_32_4 mul_32_4_5 (.a(in_1), .b(bitselector_5_out), .\输出 (\mul_32_4_5_输出 ), .\溢出判断 (\mul_32_4_5_溢出判断 ));
  MUL_32_4 mul_32_4_6 (.a(in_1), .b(bitselector_6_out), .\输出 (\mul_32_4_6_输出 ), .\溢出判断 (\mul_32_4_6_溢出判断 ));
  MUL_32_4 mul_32_4_7 (.a(in_1), .b(bitselector_7_out), .\输出 (\mul_32_4_7_输出 ), .\溢出判断 (\mul_32_4_7_溢出判断 ));
  MUL_32_4 mul_32_4_8 (.a(in_1), .b(bitselector_8_out), .\输出 (\mul_32_4_8_输出 ), .\溢出判断 (\mul_32_4_8_溢出判断 ));
  Shifter #(.width(32), .shift("ll")) shifter_1 (.in(\mul_32_4_2_输出 ), .\dist (5'b00100), .out(shifter_1_out));
  Shifter #(.width(32), .shift("ll")) shifter_2 (.in(\mul_32_4_3_输出 ), .\dist (5'b01000), .out(shifter_2_out));
  Shifter #(.width(32), .shift("ll")) shifter_3 (.in(\mul_32_4_4_输出 ), .\dist (5'b01100), .out(shifter_3_out));
  Shifter #(.width(32), .shift("ll")) shifter_4 (.in(\mul_32_4_5_输出 ), .\dist (5'b10000), .out(shifter_4_out));
  Shifter #(.width(32), .shift("ll")) shifter_5 (.in(\mul_32_4_6_输出 ), .\dist (5'b10100), .out(shifter_5_out));
  Shifter #(.width(32), .shift("ll")) shifter_6 (.in(\mul_32_4_7_输出 ), .\dist (5'b11000), .out(shifter_6_out));
  Shifter #(.width(32), .shift("ll")) shifter_7 (.in(\mul_32_4_8_输出 ), .\dist (5'b11100), .out(shifter_7_out));
  Adder #(.width(32)) adder_1 (.a(\mul_32_4_1_输出 ), .b(shifter_1_out), .out(adder_1_out));  // open: cin, cout
  or or_1 (\溢出判断 , \mul_32_4_1_溢出判断 , \mul_32_4_2_溢出判断 , \mul_32_4_3_溢出判断 , \mul_32_4_4_溢出判断 , \mul_32_4_5_溢出判断 , \mul_32_4_6_溢出判断 , \mul_32_4_7_溢出判断 , \mul_32_4_8_溢出判断 );
  Adder #(.width(32)) adder_2 (.a(adder_1_out), .b(shifter_2_out), .out(adder_2_out));  // open: cin, cout
  Adder #(.width(32)) adder_3 (.a(adder_2_out), .b(shifter_3_out), .out(adder_3_out));  // open: cin, cout
  Adder #(.width(32)) adder_4 (.a(adder_3_out), .b(shifter_4_out), .out(adder_4_out));  // open: cin, cout
  Adder #(.width(32)) adder_5 (.a(adder_4_out), .b(shifter_5_out), .out(adder_5_out));  // open: cin, cout
  Adder #(.width(32)) adder_6 (.a(adder_5_out), .b(shifter_6_out), .out(adder_6_out));  // open: cin, cout
  Adder #(.width(32)) adder_7 (.a(adder_6_out), .b(shifter_7_out), .out(out_3));  // open: cin, cout
endmodule
