// Logisim project 2 除法器.circ as structural Verilog: 6 circuits, main circuit 四位除法器
module \四位除法器  (
  input  [3:0] d,
  input  [3:0] n2,
  output \除数为0 ,
  output [3:0] rem_n2,
  output [3:0] quote_n1
);

  wire comparator_1_eq, comparator_2_eq, comparator_2_lt, comparator_3_eq, comparator_3_lt, comparator_4_eq,
       comparator_4_lt, comparator_5_eq, comparator_5_lt, or_1_out, or_2_out, or_3_out, or_4_out;
  wire [3:0] bitselector_1_out, bitselector_2_out, bitselector_3_out, bitselector_4_out, bitselector_5_out,
       bitselector_6_out, bitselector_7_out, bitselector_8_out, multiplexer_2_out, multiplexer_3_out,
       multiplexer_4_out, multiplexer_5_out, multiplexer_6_out, multiplexer_7_out, multiplexer_8_out,
       multiplexer_9_out, subtractor_1_out, subtractor_2_out, subtractor_3_out, subtractor_4_out;
  wire [7:0] bit_extender_1_out, shifter_1_out, shifter_2_out, shifter_3_out, shifter_4_out;

  Comparator #(.width(4), .mode("twosComplement")) comparator_1 (
    .a(d), .b(4'b0000), .eq(comparator_1_eq));  // open: gt, lt
  Multiplexer #(.select(1), .width(1), .disabled("Z"), .enable("false")) multiplexer_1 (
    .in0(1'b0), .in1(1'b1), .out(\除数为0 ), .sel(comparator_1_eq));
  assign bit_extender_1_out = {{4{1'b0}}, n2};  // Bit_Extender bit_extender_1
  Shifter #(.width(8), .shift("ll")) shifter_1 (.in(bit_extender_1_out), .\dist (3'b001), .out(shifter_1_out));
  Comparator #(.width(4), .mode("unsigned")) comparator_2 (
    .a(d), .b(bitselector_1_out), .eq(comparator_2_eq), .lt(comparator_2_lt));  // open: gt
  BitSelector #(.width(8), .group(4)) bitselector_1 (.in(shifter_1_out), .out(bitselector_1_out), .sel(1'b1));
  BitSelector #(.width(8), .group(4)) bitselector_2 (.in(shifter_1_out), .out(bitselector_2_out), .sel(1'b0));
  Subtractor #(.width(4)) subtractor_1 (.a(bitselector_1_out), .b(d), .out(subtractor_1_out));  // open: bin, bout
  or or_1 (or_1_out, comparator_2_eq, comparator_2_lt);
  Multiplexer #(.select(1), .width(4), .disabled("Z"), .enable("false")) multiplexer_2 (
    .in0(bitselector_2_out), .in1({bitselector_2_out[3:1], 1'b1}), .out(multiplexer_2_out), .sel(or_1_out));
  Multiplexer #(.select(1), .width(4), .disabled("Z"), .enable("false")) multiplexer_3 (
    .in0(bitselector_1_out), .in1(subtractor_1_out), .out(multiplexer_3_out), .sel(or_1_out));
  Shifter #(.width(8), .shift("ll")) shifter_2 (
    .in({multiplexer_3_out, multiplexer_2_out}), .\dist (3'b001), .out(shifter_2_out));
  BitSelector #(.width(8), .group(4)) bitselector_3 (.in(shifter_2_out), .out(bitselector_3_out), .sel(1'b1));
  BitSelector #(.width(8), .group(4)) bitselector_4 (.in(shifter_2_out), .out(bitselector_4_out), .sel(1'b0));
  Subtractor #(.width(4)) subtractor_2 (.a(bitselector_3_out), .b(d), .out(subtractor_2_out));  // open: bin, bout
  Comparator #(.width(4), .mode("unsigned")) comparator_3 (
    .a(d), .b(bitselector_3_out), .eq(comparator_3_eq), .lt(comparator_3_lt));  // open: gt
  or or_2 (or_2_out, comparator_3_eq, comparator_3_lt);
  Multiplexer #(.select(1), .width(4), .disabled("Z"), .enable("false")) multiplexer_4 (
    .in0(bitselector_4_out), .in1({bitselector_4_out[3:1], 1'b1}), .out(multiplexer_4_out), .sel(or_2_out));
  Multiplexer #(.select(1), .width(4), .disabled("Z"), .enable("false")) multiplexer_5 (
    .in0(bitselector_3_out), .in1(subtractor_2_out), .out(multiplexer_5_out), .sel(or_2_out));
  Shifter #(.width(8), .shift("ll")) shifter_3 (
    .in({multiplexer_5_out, multiplexer_4_out}), .\dist (3'b001), .out(shifter_3_out));
  BitSelector #(.width(8), .group(4)) bitselector_5 (.in(shifter_3_out), .out(bitselector_5_out), .sel(1'b1));
  BitSelector #(.width(8), .group(4)) bitselector_6 (.in(shifter_3_out), .out(bitselector_6_out), .sel(1'b0));
  Comparator #(.width(4), .mode("unsigned")) comparator_4 (
    .a(d), .b(bitselector_5_out), .eq(comparator_4_eq), .lt(comparator_4_lt));  // open: gt
  Multiplexer #(.select(1), .width(4), .disabled("Z"), .enable("false")) multiplexer_6 (
    .in0(bitselector_6_out), .in1({bitselector_6_out[3:1], 1'b1}), .out(multiplexer_6_out), .sel(or_3_out));
  Subtractor #(.width(4)) subtractor_3 (.a(bitselector_5_out), .b(d), .out(subtractor_3_out));  // open: bin, bout
  Multiplexer #(.select(1), .width(4), .disabled("Z"), .enable("false")) multiplexer_7 (
    .in0(bitselector_5_out), .in1(subtractor_3_out), .out(multiplexer_7_out), .sel(or_3_out));
  or or_3 (or_3_out, comparator_4_eq, comparator_4_lt);
  Shifter #(.width(8), .shift("ll")) shifter_4 (
    .in({multiplexer_7_out, multiplexer_6_out}), .\dist (3'b001), .out(shifter_4_out));
  BitSelector #(.width(8), .group(4)) bitselector_7 (.in(shifter_4_out), .out(bitselector_7_out), .sel(1'b1));
  BitSelector #(.width(8), .group(4)) bitselector_8 (.in(shifter_4_out), .out(bitselector_8_out), .sel(1'b0));
  Comparator #(.width(4), .mode("unsigned")) comparator_5 (
    .a(d), .b(bitselector_7_out), .eq(comparator_5_eq), .lt(comparator_5_lt));  // open: gt
  Multiplexer #(.select(1), .width(4), .disabled("Z"), .enable("false")) multiplexer_8 (
    .in0(bitselector_8_out), .in1({bitselector_8_out[3:1], 1'b1}), .out(multiplexer_8_out), .sel(or_4_out));
  Subtractor #(.width(4)) subtractor_4 (.a(bitselector_7_out), .b(d), .out(subtractor_4_out));  // open: bin, bout
  Multiplexer #(.select(1), .width(4), .disabled("Z"), .enable("false")) multiplexer_9 (
    .in0(bitselector_7_out), .in1(subtractor_4_out), .out(multiplexer_9_out), .sel(or_4_out));
  or or_4 (or_4_out, comparator_5_eq, comparator_5_lt);
  Multiplexer #(.select(1), .width(4), .disabled("Z"), .enable("false")) multiplexer_10 (
    .in0(multiplexer_9_out), .in1(4'b0000), .out(rem_n2), .sel(\除数为0 ));
  Multiplexer #(.select(1), .width(4), .disabled("Z"), .enable("false")) multiplexer_11 (
    .in0(multiplexer_8_out), .in1(4'b0000), .out(quote_n1), .sel(\除数为0 ));
endmodule

module \四位除法器测试电路  (
  input  [3:0] in_1,
  input  [3:0] in_2,
  output out_3,
  output [3:0] out_4,
  output [3:0] out_5
);

  \四位除法器  \u_四位除法器_1  (.d(in_2), .n2(in_1), .\除数为0 (out_3), .rem_n2(out_5), .quote_n1(out_4));
endmodule

module \_32位除法器  (
  input  [31:0] d,
  input  [31:0] n2,
  output [31:0] n2_rem,
  output [31:0] n1_quote,
  output \错误 
);

  wire div_8_1_error, div_8_2_error, div_8_3_error, div_8_4_error;
  wire [31:0] div_8_1_d_2, div_8_1_n1_quote, div_8_1_n2_rem, div_8_2_d_2, div_8_2_n1_quote, div_8_2_n2_rem,
       div_8_3_d_2, div_8_3_n1_quote, div_8_3_n2_rem, div_8_4_d_2, div_8_4_n1_quote, div_8_4_n2_rem;

  div_8 div_8_1 (
    .d(d), .n2(n2), .n1({32{1'b0}}), .ERROR(div_8_1_error), .d_2(div_8_1_d_2), .n1_quote(div_8_1_n1_quote),
    .n2_rem(div_8_1_n2_rem));
  // Probe on div_8_1_d_2
  div_8 div_8_2 (
    .d(div_8_1_d_2), .n2(div_8_1_n1_quote), .n1(div_8_1_n2_rem), .ERROR(div_8_2_error), .d_2(div_8_2_d_2),
    .n1_quote(div_8_2_n1_quote), .n2_rem(div_8_2_n2_rem));
  // Probe on div_8_1_n1_quote
  // Probe on div_8_2_d_2
  div_8 div_8_3 (
    .d(div_8_2_d_2), .n2(div_8_2_n1_quote), .n1(div_8_2_n2_rem), .ERROR(div_8_3_error), .d_2(div_8_3_d_2),
    .n1_quote(div_8_3_n1_quote), .n2_rem(div_8_3_n2_rem));
  or or_1 (\错误 , div_8_1_error, div_8_2_error, div_8_3_error, div_8_4_error);
  // Probe on div_8_3_d_2
  div_8 div_8_4 (
    .d(div_8_3_d_2), .n2(div_8_3_n1_quote), .n1(div_8_3_n2_rem), .ERROR(div_8_4_error), .d_2(div_8_4_d_2),
    .n1_quote(div_8_4_n1_quote), .n2_rem(div_8_4_n2_rem));
  // Probe on div_8_4_d_2
  Multiplexer #(.select(1), .width(32), .disabled("Z"), .enable("false")) multiplexer_1 (
    .in0(div_8_4_n1_quote), .in1({32{1'b0}}), .out(n2_rem), .sel(\错误 ));
  Multiplexer #(.select(1), .width(32), .disabled("Z"), .enable("false")) multiplexer_2 (
    .in0(div_8_4_n2_rem), .in1({32{1'b0}}), .out(n1_quote), .sel(\错误 ));
endmodule

module \_32位除法器测试电路  (
  input  [31:0] in_1,
  input  [31:0] in_2,
  output [31:0] out_3,
  output out_4,
  output [31:0] out_5
);

  \_32位除法器  \u_32位除法器_1  (.d(in_2), .n2(in_1), .n1_quote(out_5), .n2_rem(out_3), .\错误 (out_4));
endmodule

module div_1 (
  input  [31:0] d,
  input  [31:0] n1,
  input  [31:0] n2,
  output \除数为0 ,
  output [31:0] d_2,
  output [31:0] n1_2,
  output [31:0] n2_2
);

  wire bitselector_1_out, comparator_2_eq, comparator_2_lt, or_3_out;
  wire [31:0] bit_extender_1_out, or_1_out, or_2_out, shifter_1_out, shifter_2_out, subtractor_1_out;

  Shifter #(.width(32), .shift("ll")) shifter_1 (.in(n1), .\dist (5'b00001), .out(shifter_1_out));
  BitSelector #(.width(32), .group(1)) bitselector_1 (.in(n2), .out(bitselector_1_out), .sel({5{1'b1}}));
  Shifter #(.width(32), .shift("ll")) shifter_2 (.in(n2), .\dist (5'b00001), .out(shifter_2_out));
  Comparator #(.width(32), .mode("twosComplement")) comparator_1 (.a({32{1'b0}}), .b(d), .eq(\除数为0 ));  // open: gt, lt
  assign bit_extender_1_out = {{31{1'b0}}, bitselector_1_out};  // Bit_Extender bit_extender_1
  assign or_1_out = shifter_1_out | bit_extender_1_out;  // OR_Gate or_1, 32 bits wide
  // Probe on or_1_out
  assign or_2_out = shifter_2_out | 32'h1;  // OR_Gate or_2, 32 bits wide
  Comparator #(.width(32), .mode("unsigned")) comparator_2 (
    .a(d), .b(or_1_out), .eq(comparator_2_eq), .lt(comparator_2_lt));  // open: gt
  Subtractor #(.width(32)) subtractor_1 (.a(or_1_out), .b(d), .out(subtractor_1_out));  // open: bin, bout
  or or_3 (or_3_out, comparator_2_eq, comparator_2_lt);
  Multiplexer #(.select(1), .width(32), .disabled("Z"), .enable("false")) multiplexer_1 (
    .in0(or_1_out), .in1(subtractor_1_out), .out(n1_2), .sel(or_3_out));
  Multiplexer #(.select(1), .width(32), .disabled("Z"), .enable("false")) multiplexer_2 (
    .in0(shifter_2_out), .in1(or_2_out), .out(n2_2), .sel(or_3_out));

  assign d_2 = d;

  // Notes on the sheet:
  //   感觉不用比较器 直接看减法器的负数就行
endmodule

module div_8 (
  input  [31:0] d,
  input  [31:0] n2,
  input  [31:0] n1,
  output [31:0] d_2,
  output [31:0] n1_quote,
  output [31:0] n2_rem,
  output ERROR
);

  wire \div_1_1_除数为0 , \div_1_2_除数为0 , \div_1_3_除数为0 , \div_1_4_除数为0 , \div_1_5_除数为0 , \div_1_6_除数为0 ,
       \div_1_7_除数为0 , \div_1_8_除数为0 , or_1_out, or_3_out;
  wire [31:0] div_1_1_d_2, div_1_1_n1_2, div_1_1_n2_2, div_1_2_d_2, div_1_2_n1_2, div_1_2_n2_2, div_1_3_d_2,
       div_1_3_n1_2, div_1_3_n2_2, div_1_4_d_2, div_1_4_n1_2, div_1_4_n2_2, div_1_5_d_2, div_1_5_n1_2,
       div_1_5_n2_2, div_1_6_d_2, div_1_6_n1_2, div_1_6_n2_2, div_1_7_d_2, div_1_7_n1_2, div_1_7_n2_2;

  div_1 div_1_1 (
    .d(d), .n1(n1), .n2(n2), .\除数为0 (\div_1_1_除数为0 ), .d_2(div_1_1_d_2), .n1_2(div_1_1_n1_2),
    .n2_2(div_1_1_n2_2));
  div_1 div_1_2 (
    .d(div_1_1_d_2), .n1(div_1_1_n1_2), .n2(div_1_1_n2_2), .\除数为0 (\div_1_2_除数为0 ), .d_2(div_1_2_d_2),
    .n1_2(div_1_2_n1_2), .n2_2(div_1_2_n2_2));
  div_1 div_1_3 (
    .d(div_1_2_d_2), .n1(div_1_2_n1_2), .n2(div_1_2_n2_2), .\除数为0 (\div_1_3_除数为0 ), .d_2(div_1_3_d_2),
    .n1_2(div_1_3_n1_2), .n2_2(div_1_3_n2_2));
  or or_1 (or_1_out, \div_1_1_除数为0 , \div_1_2_除数为0 , \div_1_3_除数为0 , \div_1_4_除数为0 );
  div_1 div_1_4 (
    .d(div_1_3_d_2), .n1(div_1_3_n1_2), .n2(div_1_3_n2_2), .\除数为0 (\div_1_4_除数为0 ), .d_2(div_1_4_d_2),
    .n1_2(div_1_4_n1_2), .n2_2(div_1_4_n2_2));
  or or_2 (ERROR, or_1_out, or_3_out);
  div_1 div_1_5 (
    .d(div_1_4_d_2), .n1(div_1_4_n1_2), .n2(div_1_4_n2_2), .\除数为0 (\div_1_5_除数为0 ), .d_2(div_1_5_d_2),
    .n1_2(div_1_5_n1_2), .n2_2(div_1_5_n2_2));
  div_1 div_1_6 (
    .d(div_1_5_d_2), .n1(div_1_5_n1_2), .n2(div_1_5_n2_2), .\除数为0 (\div_1_6_除数为0 ), .d_2(div_1_6_d_2),
    .n1_2(div_1_6_n1_2), .n2_2(div_1_6_n2_2));
  div_1 div_1_7 (
    .d(div_1_6_d_2), .n1(div_1_6_n1_2), .n2(div_1_6_n2_2), .\除数为0 (\div_1_7_除数为0 ), .d_2(div_1_7_d_2),
    .n1_2(div_1_7_n1_2), .n2_2(div_1_7_n2_2));
  or or_3 (or_3_out, \div_1_5_除数为0 , \div_1_6_除数为0 , \div_1_7_除数为0 , \div_1_8_除数为0 );
  div_1 div_1_8 (
    .d(div_1_7_d_2), .n1(div_1_7_n1_2), .n2(div_1_7_n2_2), .\除数为0 (\div_1_8_除数为0 ), .d_2(d_2), .n1_2(n2_rem),
    .n2_2(n1_quote));
endmodule
