// Logisim project 4 门禁系统.circ as structural Verilog: 11 circuits, main circuit 四位二进制可逆计数器
module \四位二进制可逆计数器  (
  input  CPU,
  input  CPD,
  input  A,
  input  B,
  input  C,
  input  D,
  input  nLD,
  input  CLR,
  output QA,
  output QB,
  output QC,
  output QD
);

  wire and_1_out, and_2_out, and_3_out, and_4_out, and_5_out, and_6_out, and_7_out, and_8_out, and_9_out,
       and_10_out, and_11_out, and_12_out, and_13_out, and_14_out, d_ff_1_qn, d_ff_2_qn, d_ff_3_qn,
       d_ff_4_qn, not_1_out, not_2_out, not_3_out, not_4_out, not_5_out, or_1_out, or_2_out, or_3_out,
       or_4_out, or_5_out, or_6_out, or_7_out, or_8_out;

  or or_1 (or_1_out, CPU, CPD);
  and and_1 (and_1_out, CPU, QA);
  and and_2 (and_2_out, CPD, d_ff_1_qn);
  and and_3 (and_3_out, CPU, QA, QB);
  and and_4 (and_4_out, CPD, d_ff_1_qn, d_ff_2_qn);
  and and_5 (and_5_out, CPU, QC, QA, QB);
  and and_6 (and_6_out, CPD, d_ff_1_qn, d_ff_2_qn, d_ff_3_qn);
  or or_2 (or_2_out, and_1_out, and_2_out);
  or or_3 (or_3_out, and_3_out, and_4_out);
  or or_4 (or_4_out, and_5_out, and_6_out);
  D_Flip_Flop #(.trigger("falling"), .Pre_Clr_Positions("LEGACY"), .NegatePresetClear("false"), .enable("true"), .NewFFLayout("true")) d_ff_1 (
    .clk(or_1_out), .D(d_ff_1_qn), .Q(QA), .Qn(d_ff_1_qn), .preset(and_8_out), .en(not_1_out),
    .reset(or_5_out));
  or or_5 (or_5_out, and_7_out, CLR);
  D_Flip_Flop #(.trigger("falling"), .Pre_Clr_Positions("LEGACY"), .NegatePresetClear("false"), .enable("true"), .NewFFLayout("true")) d_ff_2 (
    .clk(or_2_out), .D(d_ff_2_qn), .Q(QB), .Qn(d_ff_2_qn), .preset(and_10_out), .en(not_1_out),
    .reset(or_6_out));
  or or_6 (or_6_out, and_9_out, CLR);
  D_Flip_Flop #(.trigger("falling"), .Pre_Clr_Positions("LEGACY"), .NegatePresetClear("false"), .enable("true"), .NewFFLayout("true")) d_ff_3 (
    .clk(or_3_out), .D(d_ff_3_qn), .Q(QC), .Qn(d_ff_3_qn), .preset(and_12_out), .en(not_1_out),
    .reset(or_7_out));
  or or_7 (or_7_out, and_11_out, CLR);
  D_Flip_Flop #(.trigger("falling"), .Pre_Clr_Positions("LEGACY"), .NegatePresetClear("false"), .enable("true"), .NewFFLayout("true")) d_ff_4 (
    .clk(or_4_out), .D(d_ff_4_qn), .Q(QD), .Qn(d_ff_4_qn), .preset(and_14_out), .en(not_1_out),
    .reset(or_8_out));
  or or_8 (or_8_out, and_13_out, CLR);
  not not_1 (not_1_out, nLD);
  and and_7 (and_7_out, not_2_out, nLD);
  and and_8 (and_8_out, A, nLD);
  and and_9 (and_9_out, not_3_out, nLD);
  and and_10 (and_10_out, B, nLD);
  and and_11 (and_11_out, not_4_out, nLD);
  and and_12 (and_12_out, C, nLD);
  and and_13 (and_13_out, not_5_out, nLD);
  and and_14 (and_14_out, D, nLD);
  not not_2 (not_2_out, A);
  not not_3 (not_3_out, B);
  not not_4 (not_4_out, C);
  not not_5 (not_5_out, D);

  // Notes on the sheet:
  //   增加
  //   减少
  //   LD输入1时重置
endmodule

module \四位二进制可逆计数器测试电路  (
  input  in_1,
  input  in_2,
  input  in_3,
  input  in_4,
  input  in_5,
  input  in_6,
  input  in_7,
  input  in_8,
  output out_9,
  output out_10,
  output out_11,
  output out_12
);

  \四位二进制可逆计数器  \u_四位二进制可逆计数器_1  (
    .CPU(in_1), .CPD(in_3), .QA(out_12), .A(in_7), .QB(out_11), .B(in_6), .QC(out_10), .C(in_5), .QD(out_9),
    .D(in_4), .nLD(in_8), .CLR(in_2));
endmodule

module \二进制转8421码电路  (
  input  QA,
  input  QB,
  input  QC,
  input  QD,
  output d1,
  output d2,
  output d5,
  output d4,
  output d3,
  output d6,
  output d7,
  output d8
);

  wire and_1_out, and_2_out, and_3_out, and_4_out, not_1_out, not_2_out, not_3_out;

  not not_1 (not_1_out, QC);
  and and_1 (and_1_out, QB, not_1_out, QD);
  and and_2 (and_2_out, QC, QD);
  or or_1 (d5, and_1_out, and_2_out);
  xor xor_1 (d2, QB, d5);
  not not_2 (not_2_out, d5);
  and and_3 (and_3_out, not_2_out, QC);
  and and_4 (and_4_out, d5, QB, QC);
  not not_3 (not_3_out, d5);
  and and_5 (d4, not_3_out, QD);
  or or_2 (d3, and_3_out, and_4_out);

  assign d1 = QA;
  assign d6 = 1'b0;
  assign d7 = 1'b0;
  assign d8 = 1'b0;

  // Notes on the sheet:
  //   101d
  //   11dd
  //   进位
endmodule

module \加法转码器  (
  input  A3,
  input  A2,
  input  A1,
  input  A0,
  output S7,
  output S6,
  output S5,
  output S4,
  output S3,
  output S2,
  output S1,
  output S0
);

  wire or_1_out;

  or or_1 (or_1_out, A2, A1);
  and and_1 (S4, or_1_out, A3);
  \先行进位四位二进制加法器  \u_先行进位四位二进制加法器_1  (
    .C0(1'b0), .A0(A0), .B0(1'b0), .A1(A1), .B1(S4), .A2(A2), .B2(S4), .A3(A3), .B3(1'b0), .S0(S0), .S1(S1),
    .S2(S2), .S3(S3));  // open: C4

  assign S5 = 1'b0;
  assign S6 = 1'b0;
  assign S7 = 1'b0;
endmodule

module \二进制转8421码测试电路  (
  input  in_1,
  input  in_2,
  input  in_3,
  input  in_4,
  input  in_5,
  input  in_6,
  input  in_7,
  input  in_8
);

  wire \四位二进制可逆计数器_1_qa , \四位二进制可逆计数器_1_qb , \四位二进制可逆计数器_1_qc , \四位二进制可逆计数器_1_qd ;

  \四位二进制可逆计数器  \u_四位二进制可逆计数器_1  (
    .CPU(in_1), .CPD(in_3), .QA(\四位二进制可逆计数器_1_qa ), .A(in_7), .QB(\四位二进制可逆计数器_1_qb ), .B(in_6),
    .QC(\四位二进制可逆计数器_1_qc ), .C(in_5), .QD(\四位二进制可逆计数器_1_qd ), .D(in_4), .nLD(in_8), .CLR(in_2));
  \二进制转8421码电路  \u_二进制转8421码电路_1  (
    .QA(\四位二进制可逆计数器_1_qa ), .QB(\四位二进制可逆计数器_1_qb ), .QC(\四位二进制可逆计数器_1_qc ), .QD(\四位二进制可逆计数器_1_qd ));  // open: d1, d2, d5, d4, d3, d6, d7, d8
endmodule

module \译码器  (
  input  A3,
  input  A2,
  input  A1,
  input  A0,
  output a,
  output b,
  output c,
  output d,
  output e,
  output f,
  output g
);

  wire and_1_out, and_2_out, and_3_out, and_4_out, and_5_out, and_6_out, and_7_out, and_8_out, and_9_out,
       and_10_out, and_11_out, and_12_out, and_13_out, and_14_out, and_15_out, and_16_out, and_17_out,
       and_18_out, and_19_out, and_20_out, and_21_out, and_22_out, and_23_out, and_24_out, and_25_out,
       not_1_out, not_2_out, not_3_out, not_4_out, not_5_out, not_6_out, not_7_out, not_8_out, not_9_out,
       not_10_out, not_11_out, not_12_out, not_13_out, not_14_out, not_15_out, not_16_out, not_17_out,
       not_18_out, not_19_out, not_20_out, not_21_out, not_22_out, not_23_out, not_24_out, not_25_out,
       not_26_out, not_27_out, not_28_out, not_29_out, not_30_out, not_31_out, not_32_out, not_33_out,
       not_34_out, not_35_out, not_36_out, not_37_out, not_38_out, not_39_out, not_40_out, not_41_out,
       not_42_out, not_43_out, not_44_out, not_45_out, not_46_out, not_47_out, not_48_out, not_49_out,
       not_50_out, not_51_out;

  not not_1 (not_1_out, A3);
  not not_2 (not_2_out, A2);
  and and_1 (and_1_out, not_1_out, not_2_out, not_3_out);
  not not_3 (not_3_out, A0);
  not not_4 (not_4_out, A3);
  not not_5 (not_5_out, A2);
  and and_2 (and_2_out, not_4_out, not_5_out, A1);
  not not_6 (not_6_out, A3);
  and and_3 (and_3_out, not_6_out, A2, A0);
  and and_4 (and_4_out, A3, not_7_out, not_8_out);
  not not_7 (not_7_out, A2);
  not not_8 (not_8_out, A1);
  not not_9 (not_9_out, A3);
  and and_5 (and_5_out, not_9_out, not_10_out);
  not not_10 (not_10_out, A2);
  not not_11 (not_11_out, A3);
  and and_6 (and_6_out, not_11_out, not_12_out, not_13_out);
  not not_12 (not_12_out, A1);
  not not_13 (not_13_out, A0);
  not not_14 (not_14_out, A2);
  and and_7 (and_7_out, not_14_out, not_15_out);
  not not_15 (not_15_out, A1);
  not not_16 (not_16_out, A3);
  and and_8 (and_8_out, not_16_out, A1, A0);
  not not_17 (not_17_out, A2);
  and and_9 (and_9_out, not_17_out, not_18_out);
  not not_18 (not_18_out, A1);
  not not_19 (not_19_out, A3);
  and and_10 (and_10_out, not_19_out, A0);
  not not_20 (not_20_out, A3);
  and and_11 (and_11_out, not_20_out, A2);
  not not_21 (not_21_out, A2);
  not not_22 (not_22_out, A1);
  not not_23 (not_23_out, A0);
  not not_24 (not_24_out, A3);
  not not_25 (not_25_out, A2);
  not not_26 (not_26_out, A3);
  not not_27 (not_27_out, A0);
  not not_28 (not_28_out, A3);
  not not_29 (not_29_out, A1);
  not not_30 (not_30_out, A2);
  and and_12 (and_12_out, not_30_out, not_31_out, not_32_out);
  not not_31 (not_31_out, A1);
  not not_32 (not_32_out, A0);
  not not_33 (not_33_out, A3);
  and and_13 (and_13_out, not_33_out, A1, not_34_out);
  not not_34 (not_34_out, A0);
  not not_35 (not_35_out, A3);
  and and_14 (and_14_out, not_35_out, not_36_out, not_37_out);
  not not_36 (not_36_out, A1);
  not not_37 (not_37_out, A0);
  not not_38 (not_38_out, A3);
  and and_15 (and_15_out, not_38_out, A2, not_39_out);
  not not_39 (not_39_out, A1);
  not not_40 (not_40_out, A3);
  and and_16 (and_16_out, not_40_out, A2, not_41_out);
  not not_41 (not_41_out, A0);
  and and_17 (and_17_out, A3, not_42_out, not_43_out);
  not not_42 (not_42_out, A2);
  not not_43 (not_43_out, A1);
  not not_44 (not_44_out, A3);
  not not_45 (not_45_out, A2);
  and and_18 (and_18_out, not_44_out, not_45_out, A1);
  not not_46 (not_46_out, A3);
  and and_19 (and_19_out, not_46_out, A2, not_47_out);
  not not_47 (not_47_out, A1);
  not not_48 (not_48_out, A3);
  and and_20 (and_20_out, not_48_out, A2, not_49_out);
  not not_49 (not_49_out, A0);
  not not_50 (not_50_out, A2);
  and and_21 (and_21_out, A3, not_50_out, not_51_out);
  not not_51 (not_51_out, A1);
  or or_1 (a, and_1_out, and_2_out, and_3_out, and_4_out);
  or or_2 (b, and_5_out, and_6_out, and_7_out, and_8_out);
  or or_3 (c, and_9_out, and_10_out, and_11_out);
  and and_22 (and_22_out, not_21_out, not_22_out, not_23_out);
  and and_23 (and_23_out, not_24_out, not_25_out, A1);
  and and_24 (and_24_out, not_26_out, A1, not_27_out);
  and and_25 (and_25_out, not_28_out, A2, not_29_out, A0);
  or or_4 (e, and_12_out, and_13_out);
  or or_5 (f, and_14_out, and_15_out, and_16_out, and_17_out);
  or or_6 (g, and_18_out, and_19_out, and_20_out, and_21_out);
  or or_7 (d, and_22_out, and_23_out, and_24_out, and_25_out);
endmodule

module \显示电路测试电路  (
  input  in_1,
  input  in_2,
  input  in_3,
  input  in_4,
  input  in_5,
  input  in_6,
  input  in_7,
  input  in_8
);

  wire \二进制转8421码电路_1_d1 , \二进制转8421码电路_1_d2 , \二进制转8421码电路_1_d3 , \二进制转8421码电路_1_d4 , \二进制转8421码电路_1_d5 ,
       \二进制转8421码电路_1_d6 , \二进制转8421码电路_1_d7 , \二进制转8421码电路_1_d8 , \四位二进制可逆计数器_1_qa , \四位二进制可逆计数器_1_qb ,
       \四位二进制可逆计数器_1_qc , \四位二进制可逆计数器_1_qd , \译码器_1_a , \译码器_1_b , \译码器_1_c , \译码器_1_d , \译码器_1_e ,
       \译码器_1_f , \译码器_1_g , \译码器_2_a , \译码器_2_b , \译码器_2_c , \译码器_2_d , \译码器_2_e , \译码器_2_f , \译码器_2_g ;

  \四位二进制可逆计数器  \u_四位二进制可逆计数器_1  (
    .CPU(in_1), .CPD(in_3), .QA(\四位二进制可逆计数器_1_qa ), .A(in_7), .QB(\四位二进制可逆计数器_1_qb ), .B(in_6),
    .QC(\四位二进制可逆计数器_1_qc ), .C(in_5), .QD(\四位二进制可逆计数器_1_qd ), .D(in_4), .nLD(in_8), .CLR(in_2));
  \二进制转8421码电路  \u_二进制转8421码电路_1  (
    .QA(\四位二进制可逆计数器_1_qa ), .QB(\四位二进制可逆计数器_1_qb ), .QC(\四位二进制可逆计数器_1_qc ), .QD(\四位二进制可逆计数器_1_qd ),
    .d1(\二进制转8421码电路_1_d1 ), .d2(\二进制转8421码电路_1_d2 ), .d5(\二进制转8421码电路_1_d5 ), .d4(\二进制转8421码电路_1_d4 ),
    .d3(\二进制转8421码电路_1_d3 ), .d6(\二进制转8421码电路_1_d6 ), .d7(\二进制转8421码电路_1_d7 ), .d8(\二进制转8421码电路_1_d8 ));
  \译码器  \u_译码器_1  (
    .A3(\二进制转8421码电路_1_d4 ), .A2(\二进制转8421码电路_1_d3 ), .A1(\二进制转8421码电路_1_d2 ), .A0(\二进制转8421码电路_1_d1 ),
    .a(\译码器_1_a ), .b(\译码器_1_b ), .c(\译码器_1_c ), .d(\译码器_1_d ), .e(\译码器_1_e ), .f(\译码器_1_f ), .g(\译码器_1_g ));
  \译码器  \u_译码器_2  (
    .A3(\二进制转8421码电路_1_d8 ), .A2(\二进制转8421码电路_1_d7 ), .A1(\二进制转8421码电路_1_d6 ), .A0(\二进制转8421码电路_1_d5 ),
    .a(\译码器_2_a ), .b(\译码器_2_b ), .c(\译码器_2_c ), .d(\译码器_2_d ), .e(\译码器_2_e ), .f(\译码器_2_f ), .g(\译码器_2_g ));
  _7_Segment_Display #(.active("true")) u_7_segment_display_1 (
    .g(\译码器_1_g ), .f(\译码器_1_f ), .a(\译码器_1_a ), .b(\译码器_1_b ), .e(\译码器_1_e ), .d(\译码器_1_d ), .c(\译码器_1_c ));  // open: dp
  _7_Segment_Display #(.active("true")) u_7_segment_display_2 (
    .g(\译码器_2_g ), .f(\译码器_2_f ), .a(\译码器_2_a ), .b(\译码器_2_b ), .e(\译码器_2_e ), .d(\译码器_2_d ), .c(\译码器_2_c ));  // open: dp
endmodule

module \有报警功能的计数器  (
  input  \刷入 ,
  input  in_2,
  input  \刷出 ,
  input  in_4,
  input  in_5,
  input  in_6,
  input  in_7,
  input  in_8,
  output QA,
  output QB,
  output \满员警告 ,
  output QC,
  output QD
);

  wire and_2_out, and_3_out, and_4_out, nor_1_out, not_1_out, not_2_out;

  not not_1 (not_1_out, and_4_out);
  not not_2 (not_2_out, nor_1_out);
  and and_1 (\满员警告 , and_4_out, \刷入 );
  and and_2 (and_2_out, not_1_out, \刷入 );
  and and_3 (and_3_out, \刷出 , not_2_out);
  and and_4 (and_4_out, QD, QC, QB, QA);
  \四位二进制可逆计数器  \u_四位二进制可逆计数器_1  (
    .CPU(and_2_out), .CPD(and_3_out), .QA(QA), .A(in_7), .QB(QB), .B(in_6), .QC(QC), .C(in_5), .QD(QD),
    .D(in_4), .nLD(in_8), .CLR(in_2));
  nor nor_1 (nor_1_out, QA, QB, QC, QD);
endmodule

module \小型实验室门禁系统  (
  input  in_1,
  input  in_2,
  input  in_3,
  output out_4,
  output out_5,
  output out_6,
  output out_7,
  output out_8,
  output out_9,
  output out_10,
  output out_11,
  output out_12,
  output out_13,
  output out_14,
  output out_15,
  output out_16,
  output out_17,
  output out_18
);

  wire \二进制转8421码电路_1_d1 , \二进制转8421码电路_1_d2 , \二进制转8421码电路_1_d3 , \二进制转8421码电路_1_d4 , \二进制转8421码电路_1_d5 ,
       \二进制转8421码电路_1_d6 , \二进制转8421码电路_1_d7 , \二进制转8421码电路_1_d8 , \有报警功能的计数器_1_qa , \有报警功能的计数器_1_qb ,
       \有报警功能的计数器_1_qc , \有报警功能的计数器_1_qd ;

  \有报警功能的计数器  \u_有报警功能的计数器_1  (
    .\刷入 (in_1), .in_2(in_2), .\刷出 (in_3), .QA(\有报警功能的计数器_1_qa ), .QB(\有报警功能的计数器_1_qb ), .\满员警告 (out_16),
    .QC(\有报警功能的计数器_1_qc ), .QD(\有报警功能的计数器_1_qd ), .in_4(1'b0), .in_5(1'b0), .in_6(1'b0), .in_7(1'b0),
    .in_8(1'b0));
  \二进制转8421码电路  \u_二进制转8421码电路_1  (
    .QA(\有报警功能的计数器_1_qa ), .QB(\有报警功能的计数器_1_qb ), .QC(\有报警功能的计数器_1_qc ), .QD(\有报警功能的计数器_1_qd ),
    .d1(\二进制转8421码电路_1_d1 ), .d2(\二进制转8421码电路_1_d2 ), .d5(\二进制转8421码电路_1_d5 ), .d4(\二进制转8421码电路_1_d4 ),
    .d3(\二进制转8421码电路_1_d3 ), .d6(\二进制转8421码电路_1_d6 ), .d7(\二进制转8421码电路_1_d7 ), .d8(\二进制转8421码电路_1_d8 ));
  \译码器  \u_译码器_1  (
    .A3(\二进制转8421码电路_1_d4 ), .A2(\二进制转8421码电路_1_d3 ), .A1(\二进制转8421码电路_1_d2 ), .A0(\二进制转8421码电路_1_d1 ),
    .a(out_4), .b(out_5), .c(out_6), .d(out_7), .e(out_8), .f(out_9), .g(out_10));
  \译码器  \u_译码器_2  (
    .A3(\二进制转8421码电路_1_d8 ), .A2(\二进制转8421码电路_1_d7 ), .A1(\二进制转8421码电路_1_d6 ), .A0(\二进制转8421码电路_1_d5 ),
    .a(out_11), .b(out_12), .c(out_13), .d(out_14), .e(out_15), .f(out_17), .g(out_18));
endmodule

module \小型门禁系统测试电路  (
  input  in_1,
  input  in_2,
  input  in_3,
  output out_4
);

  wire \小型实验室门禁系统_1_out_4 , \小型实验室门禁系统_1_out_5 , \小型实验室门禁系统_1_out_6 , \小型实验室门禁系统_1_out_7 ,
       \小型实验室门禁系统_1_out_8 , \小型实验室门禁系统_1_out_9 , \小型实验室门禁系统_1_out_10 , \小型实验室门禁系统_1_out_11 ,
       \小型实验室门禁系统_1_out_12 , \小型实验室门禁系统_1_out_13 , \小型实验室门禁系统_1_out_14 , \小型实验室门禁系统_1_out_15 ,
       \小型实验室门禁系统_1_out_18 ;

  _7_Segment_Display #(.active("true")) u_7_segment_display_1 (
    .g(\小型实验室门禁系统_1_out_18 ), .f(\小型实验室门禁系统_1_out_15 ), .a(\小型实验室门禁系统_1_out_11 ), .b(\小型实验室门禁系统_1_out_12 ),
    .e(\小型实验室门禁系统_1_out_15 ), .d(\小型实验室门禁系统_1_out_14 ), .c(\小型实验室门禁系统_1_out_13 ));  // open: dp
  _7_Segment_Display #(.active("true")) u_7_segment_display_2 (
    .g(\小型实验室门禁系统_1_out_10 ), .f(\小型实验室门禁系统_1_out_9 ), .a(\小型实验室门禁系统_1_out_4 ), .b(\小型实验室门禁系统_1_out_5 ),
    .e(\小型实验室门禁系统_1_out_8 ), .d(\小型实验室门禁系统_1_out_7 ), .c(\小型实验室门禁系统_1_out_6 ));  // open: dp
  \小型实验室门禁系统  \u_小型实验室门禁系统_1  (
    .in_1(in_1), .in_2(in_2), .in_3(in_3), .out_16(out_4), .out_4(\小型实验室门禁系统_1_out_4 ),
    .out_5(\小型实验室门禁系统_1_out_5 ), .out_6(\小型实验室门禁系统_1_out_6 ), .out_7(\小型实验室门禁系统_1_out_7 ),
    .out_8(\小型实验室门禁系统_1_out_8 ), .out_11(\小型实验室门禁系统_1_out_11 ), .out_12(\小型实验室门禁系统_1_out_12 ),
    .out_13(\小型实验室门禁系统_1_out_13 ), .out_14(\小型实验室门禁系统_1_out_14 ), .out_15(\小型实验室门禁系统_1_out_15 ),
    .out_17(\小型实验室门禁系统_1_out_15 ), .out_18(\小型实验室门禁系统_1_out_18 ), .out_10(\小型实验室门禁系统_1_out_10 ),
    .out_9(\小型实验室门禁系统_1_out_9 ));
endmodule

module \先行进位四位二进制加法器  (
  input  C0,
  input  A0,
  input  B0,
  input  A1,
  input  B1,
  input  A2,
  input  B2,
  input  A3,
  input  B3,
  output S0,
  output S1,
  output S2,
  output S3,
  output C4
);

  wire and_1_out, and_2_out, and_3_out, and_4_out, and_5_out, and_6_out, and_7_out, and_8_out, and_9_out,
       and_10_out, and_11_out, and_12_out, and_13_out, and_14_out, or_1_out, or_2_out, or_3_out, xor_1_out,
       xor_2_out, xor_3_out, xor_4_out;

  xor xor_1 (xor_1_out, A0, B0);
  and and_1 (and_1_out, A0, B0);
  xor xor_2 (xor_2_out, A1, B1);
  and and_2 (and_2_out, A1, B1);
  xor xor_3 (xor_3_out, A2, B2);
  and and_3 (and_3_out, A2, B2);
  xor xor_4 (xor_4_out, A3, B3);
  and and_4 (and_4_out, A3, B3);
  and and_5 (and_5_out, C0, xor_1_out);
  and and_6 (and_6_out, and_1_out, xor_2_out);
  and and_7 (and_7_out, xor_2_out, xor_1_out, C0);
  and and_8 (and_8_out, and_2_out, xor_3_out);
  and and_9 (and_9_out, xor_3_out, xor_2_out, and_1_out);
  and and_10 (and_10_out, xor_3_out, xor_2_out, xor_1_out, C0);
  and and_11 (and_11_out, and_3_out, xor_4_out);
  and and_12 (and_12_out, and_2_out, xor_3_out, xor_4_out);
  and and_13 (and_13_out, xor_4_out, xor_3_out, xor_2_out, and_1_out);
  and and_14 (and_14_out, xor_4_out, xor_3_out, xor_2_out, xor_1_out, C0);
  or or_1 (or_1_out, and_5_out, and_1_out);
  or or_2 (or_2_out, and_6_out, and_7_out, and_2_out);
  or or_3 (or_3_out, and_8_out, and_9_out, and_10_out, and_3_out);
  or or_4 (C4, and_11_out, and_12_out, and_13_out, and_14_out, and_4_out);
  xor xor_5 (S0, C0, xor_1_out);
  xor xor_6 (S1, or_1_out, xor_2_out);
  xor xor_7 (S2, or_2_out, xor_3_out);
  xor xor_8 (S3, or_3_out, xor_4_out);

  // Notes on the sheet:
  //   P1
  //   G1
  //   P2
  //   G2
  //   P3
  //   G3
  //   P4
  //   G4
  //   C1
  //   C2
  //   C3
endmodule
