// Logisim project 5 电子钟.circ as structural Verilog: 14 circuits, main circuit 四位二进制可逆计数器
module \四位二进制可逆计数器  (
  input  CPU,
  input  CPD,
  input  A,
  input  B,
  input  C,
  input  D,
  input  nLD,
  input  CLR,
  output QA,
  output QB,
  output QC,
  output QD
);

  wire and_1_out, and_2_out, and_3_out, and_4_out, and_5_out, and_6_out, and_7_out, and_8_out, and_9_out,
       and_10_out, and_11_out, and_12_out, and_13_out, and_14_out, d_ff_1_qn, d_ff_2_qn, d_ff_3_qn,
       d_ff_4_qn, not_1_out, not_2_out, not_3_out, not_4_out, not_5_out, or_1_out, or_2_out, or_3_out,
       or_4_out, or_5_out, or_6_out, or_7_out, or_8_out;

  or or_1 (or_1_out, CPU, CPD);
  and and_1 (and_1_out, CPU, QA);
  and and_2 (and_2_out, CPD, d_ff_1_qn);
  and and_3 (and_3_out, CPU, QA, QB);
  and and_4 (and_4_out, CPD, d_ff_1_qn, d_ff_2_qn);
  and and_5 (and_5_out, CPU, QC, QA, QB);
  and and_6 (and_6_out, CPD, d_ff_1_qn, d_ff_2_qn, d_ff_3_qn);
  or or_2 (or_2_out, and_1_out, and_2_out);
  or or_3 (or_3_out, and_3_out, and_4_out);
  or or_4 (or_4_out, and_5_out, and_6_out);
  D_Flip_Flop #(.trigger("falling"), .Pre_Clr_Positions("LEGACY"), .NegatePresetClear("false"), .enable("true"), .NewFFLayout("true")) d_ff_1 (
    .clk(or_1_out), .D(d_ff_1_qn), .Q(QA), .Qn(d_ff_1_qn), .preset(and_8_out), .en(not_1_out),
    .reset(or_5_out));
  or or_5 (or_5_out, and_7_out, CLR);
  D_Flip_Flop #(.trigger("falling"), .Pre_Clr_Positions("LEGACY"), .NegatePresetClear("false"), .enable("true"), .NewFFLayout("true")) d_ff_2 (
    .clk(or_2_out), .D(d_ff_2_qn), .Q(QB), .Qn(d_ff_2_qn), .preset(and_10_out), .en(not_1_out),
    .reset(or_6_out));
  or or_6 (or_6_out, and_9_out, CLR);
  D_Flip_Flop #(.trigger("falling"), .Pre_Clr_Positions("LEGACY"), .NegatePresetClear("false"), .enable("true"), .NewFFLayout("true")) d_ff_3 (
    .clk(or_3_out), .D(d_ff_3_qn), .Q(QC), .Qn(d_ff_3_qn), .preset(and_12_out), .en(not_1_out),
    .reset(or_7_out));
  or or_7 (or_7_out, and_11_out, CLR);
  D_Flip_Flop #(.trigger("falling"), .Pre_Clr_Positions("LEGACY"), .NegatePresetClear("false"), .enable("true"), .NewFFLayout("true")) d_ff_4 (
    .clk(or_4_out), .D(d_ff_4_qn), .Q(QD), .Qn(d_ff_4_qn), .preset(and_14_out), .en(not_1_out),
    .reset(or_8_out));
  or or_8 (or_8_out, and_13_out, CLR);
  not not_1 (not_1_out, nLD);
  and and_7 (and_7_out, not_2_out, nLD);
  and and_8 (and_8_out, A, nLD);
  and and_9 (and_9_out, not_3_out, nLD);
  and and_10 (and_10_out, B, nLD);
  and and_11 (and_11_out, not_4_out, nLD);
  and and_12 (and_12_out, C, nLD);
  and and_13 (and_13_out, not_5_out, nLD);
  and and_14 (and_14_out, D, nLD);
  not not_2 (not_2_out, A);
  not not_3 (not_3_out, B);
  not not_4 (not_4_out, C);
  not not_5 (not_5_out, D);

  // Notes on the sheet:
  //   增加
  //   减少
  //   输入1时重置
endmodule

module \六十进制计数器  (
  input  CPU,
  input  CPD,
  input  ADJ,
  input  CLR,
  output \nQcc进位 ,
  output out_6,
  output out_7,
  output out_8,
  output out_9,
  output out_10,
  output out_11,
  output out_12,
  output out_13
);

  wire and_1_out, and_2_out, and_3_out, and_4_out, and_6_out, and_7_out, buffer_1_out, buffer_2_out,
       not_1_out, not_2_out, not_3_out, or_1_out, or_2_out, or_3_out, or_4_out, or_5_out, or_6_out;

  or or_1 (or_1_out, or_6_out, or_2_out);
  or or_2 (or_2_out, out_9, out_8, out_7, out_6);
  and and_1 (and_1_out, CPD, ADJ);
  and and_2 (and_2_out, or_1_out, and_1_out);
  \四位二进制可逆计数器  \u_四位二进制可逆计数器_1  (
    .CPU(CPU), .CPD(and_2_out), .QA(out_9), .A(1'b1), .QB(out_8), .B(1'b0), .QC(out_7), .C(1'b0), .QD(out_6),
    .D(1'b1), .nLD(and_3_out), .CLR(or_3_out));
  or or_3 (or_3_out, or_4_out, CLR);
  and and_3 (and_3_out, out_6, out_8, out_9, out_7);
  not not_1 (not_1_out, out_7);
  not not_2 (not_2_out, out_9);
  and and_4 (and_4_out, not_1_out, not_2_out, buffer_1_out, buffer_2_out);
  buf buffer_1 (buffer_1_out, out_8);
  buf buffer_2 (buffer_2_out, out_6);
  or or_4 (or_4_out, and_4_out, and_7_out);
  not not_3 (not_3_out, ADJ);
  and and_5 (\nQcc进位 , not_3_out, and_7_out);
  or or_5 (or_5_out, and_7_out, CLR);
  and and_6 (and_6_out, and_3_out, or_6_out);
  \四位二进制可逆计数器  \u_四位二进制可逆计数器_2  (
    .CPU(and_4_out), .CPD(and_6_out), .QA(out_13), .QB(out_12), .QC(out_11), .QD(out_10), .nLD(1'b0),
    .CLR(or_5_out));  // open: A, B, C, D
  and and_7 (and_7_out, out_11, out_12);
  or or_6 (or_6_out, out_13, out_12, out_11, out_10);

  // Notes on the sheet:
  //   实现0减不循环
  //   处理十位减1
  //   60进位个位判断
  //   退位后重置为9
  //   清零判定
  //   60进位十位判断
endmodule

module \六十进制计数器测试电路  (
  input  in_1,
  input  in_2
);

  wire button_1_out, button_2_out, button_3_out, button_4_out, clock_1_out, \六十进制计数器_1_nqcc进位 ;
  wire [3:0] \六十进制计数器_1_out_9 , \六十进制计数器_1_out_13 , \六十进制计数器_2_out_9 , \六十进制计数器_2_out_13 ;

  Clock #(.highDuration(1), .lowDuration(1)) clock_1 (.out(clock_1_out));
  Button button_1 (.out(button_1_out));
  Hex_Digit_Display hex_digit_display_1 (.value(\六十进制计数器_1_out_13 ), .dp(1'b0));
  Hex_Digit_Display hex_digit_display_2 (.value(\六十进制计数器_1_out_9 ), .dp(1'b0));
  \六十进制计数器  \u_六十进制计数器_1  (
    .CPU(clock_1_out), .CPD(button_1_out), .ADJ(in_1), .\nQcc进位 (\六十进制计数器_1_nqcc进位 ),
    .out_6(\六十进制计数器_1_out_9 [3]), .out_7(\六十进制计数器_1_out_9 [2]), .out_8(\六十进制计数器_1_out_9 [1]),
    .out_9(\六十进制计数器_1_out_9 [0]), .out_10(\六十进制计数器_1_out_13 [3]), .out_11(\六十进制计数器_1_out_13 [2]),
    .out_12(\六十进制计数器_1_out_13 [1]), .out_13(\六十进制计数器_1_out_13 [0]), .CLR(button_2_out));
  Button button_2 (.out(button_2_out));
  Button button_3 (.out(button_3_out));
  Hex_Digit_Display hex_digit_display_3 (.value(\六十进制计数器_2_out_13 ), .dp(1'b0));
  Hex_Digit_Display hex_digit_display_4 (.value(\六十进制计数器_2_out_9 ), .dp(1'b0));
  \六十进制计数器  \u_六十进制计数器_2  (
    .CPU(\六十进制计数器_1_nqcc进位 ), .CPD(button_3_out), .ADJ(in_2), .out_6(\六十进制计数器_2_out_9 [3]),
    .out_7(\六十进制计数器_2_out_9 [2]), .out_8(\六十进制计数器_2_out_9 [1]), .out_9(\六十进制计数器_2_out_9 [0]),
    .out_10(\六十进制计数器_2_out_13 [3]), .out_11(\六十进制计数器_2_out_13 [2]), .out_12(\六十进制计数器_2_out_13 [1]),
    .out_13(\六十进制计数器_2_out_13 [0]), .CLR(button_4_out));  // open: nQcc进位
  Button button_4 (.out(button_4_out));

  // Notes on the sheet:
  //   秒
  //   分
endmodule

module \十二进制计数器或二十四进制的计数器电路  (
  input  SET,
  input  CPu,
  input  ADJ,
  input  CPd,
  input  CLR,
  output out_6,
  output out_7,
  output out_8,
  output out_9,
  output out_10,
  output out_11,
  output out_12,
  output \_24进制进位 ,
  output \nQcc_进位 
);

  wire and_1_out, and_2_out, or_1_out;

  \六十进制计数器  \u_六十进制计数器_1  (
    .CPU(CPu), .CPD(CPd), .ADJ(ADJ), .out_6(out_10), .out_7(out_11), .out_8(out_12), .out_9(\_24进制进位 ),
    .out_10(out_6), .out_11(out_7), .out_12(out_8), .out_13(out_9), .CLR(or_1_out));  // open: nQcc进位
  and and_1 (and_1_out, out_11, out_8);
  and and_2 (and_2_out, out_12, out_9);
  or or_1 (or_1_out, \nQcc_进位 , CLR);
  Multiplexer #(.select(1), .width(1), .disabled("Z"), .enable("false")) multiplexer_1 (
    .in0(and_2_out), .in1(and_1_out), .out(\nQcc_进位 ), .sel(SET));

  // Notes on the sheet:
  //   SET=0 12进制 SET=1 24进制
  //   12进制进位
endmodule

module \十二进制计数器或二十四进制的计数器测试电路  (
  input  in_1,
  input  in_2,
  input  in_3,
  input  in_4,
  output out_5
);

  wire button_1_out, button_2_out, button_3_out, button_4_out, button_5_out, \十二进制计数器或二十四进制的计数器电路_1_nqcc_进位 ;
  wire [3:0] \十二进制计数器或二十四进制的计数器电路_1__24进制进位 , \十二进制计数器或二十四进制的计数器电路_1_out_9 , \十二进制计数器或二十四进制的计数器电路_2__24进制进位 ,
       \十二进制计数器或二十四进制的计数器电路_2_out_9 ;

  Button button_1 (.out(button_1_out));
  Button button_2 (.out(button_2_out));
  Hex_Digit_Display hex_digit_display_1 (.value(\十二进制计数器或二十四进制的计数器电路_1_out_9 ), .dp(1'b0));
  Hex_Digit_Display hex_digit_display_2 (.value(\十二进制计数器或二十四进制的计数器电路_1__24进制进位 ), .dp(1'b0));
  \十二进制计数器或二十四进制的计数器电路  \u_十二进制计数器或二十四进制的计数器电路_1  (
    .CPu(button_1_out), .ADJ(in_1), .CPd(button_2_out), .\nQcc_进位 (\十二进制计数器或二十四进制的计数器电路_1_nqcc_进位 ),
    .CLR(button_3_out), .out_6(\十二进制计数器或二十四进制的计数器电路_1_out_9 [3]), .out_7(\十二进制计数器或二十四进制的计数器电路_1_out_9 [2]),
    .out_8(\十二进制计数器或二十四进制的计数器电路_1_out_9 [1]), .out_9(\十二进制计数器或二十四进制的计数器电路_1_out_9 [0]),
    .out_10(\十二进制计数器或二十四进制的计数器电路_1__24进制进位 [3]), .out_11(\十二进制计数器或二十四进制的计数器电路_1__24进制进位 [2]),
    .out_12(\十二进制计数器或二十四进制的计数器电路_1__24进制进位 [1]), .\_24进制进位 (\十二进制计数器或二十四进制的计数器电路_1__24进制进位 [0]), .SET(in_2));
  Button button_3 (.out(button_3_out));
  Button button_4 (.out(button_4_out));
  Hex_Digit_Display hex_digit_display_3 (.value(\十二进制计数器或二十四进制的计数器电路_2_out_9 ), .dp(1'b0));
  Hex_Digit_Display hex_digit_display_4 (.value(\十二进制计数器或二十四进制的计数器电路_2__24进制进位 ), .dp(1'b0));
  \十二进制计数器或二十四进制的计数器电路  \u_十二进制计数器或二十四进制的计数器电路_2  (
    .CPu(\十二进制计数器或二十四进制的计数器电路_1_nqcc_进位 ), .ADJ(in_3), .CPd(button_4_out), .\nQcc_进位 (out_5),
    .CLR(button_5_out), .out_6(\十二进制计数器或二十四进制的计数器电路_2_out_9 [3]), .out_7(\十二进制计数器或二十四进制的计数器电路_2_out_9 [2]),
    .out_8(\十二进制计数器或二十四进制的计数器电路_2_out_9 [1]), .out_9(\十二进制计数器或二十四进制的计数器电路_2_out_9 [0]),
    .out_10(\十二进制计数器或二十四进制的计数器电路_2__24进制进位 [3]), .out_11(\十二进制计数器或二十四进制的计数器电路_2__24进制进位 [2]),
    .out_12(\十二进制计数器或二十四进制的计数器电路_2__24进制进位 [1]), .\_24进制进位 (\十二进制计数器或二十四进制的计数器电路_2__24进制进位 [0]), .SET(in_4));
  Button button_5 (.out(button_5_out));
endmodule

module \上下午文字显示的电路  (
  input  AM_FM,
  input  TT,
  output [4:0] out_3,
  output [4:0] out_4,
  output [4:0] out_5,
  output [4:0] out_6
);

  wire [4:0] multiplexer_1_out, multiplexer_3_out, multiplexer_5_out, multiplexer_7_out;

  Multiplexer #(.select(1), .width(5), .disabled("Z"), .enable("false")) multiplexer_1 (
    .in0(5'b00001), .in1(5'b10000), .out(multiplexer_1_out), .sel(AM_FM));
  Multiplexer #(.select(1), .width(5), .disabled("Z"), .enable("false")) multiplexer_2 (
    .in0({5{1'b0}}), .in1(multiplexer_1_out), .out(out_3), .sel(TT));
  Multiplexer #(.select(1), .width(5), .disabled("Z"), .enable("false")) multiplexer_3 (
    .in0({5{1'b1}}), .in1({5{1'b1}}), .out(multiplexer_3_out), .sel(AM_FM));
  Multiplexer #(.select(1), .width(5), .disabled("Z"), .enable("false")) multiplexer_4 (
    .in0({5{1'b0}}), .in1(multiplexer_3_out), .out(out_4), .sel(TT));
  Multiplexer #(.select(1), .width(5), .disabled("Z"), .enable("false")) multiplexer_5 (
    .in0(5'b00101), .in1(5'b10100), .out(multiplexer_5_out), .sel(AM_FM));
  Multiplexer #(.select(1), .width(5), .disabled("Z"), .enable("false")) multiplexer_6 (
    .in0({5{1'b0}}), .in1(multiplexer_5_out), .out(out_5), .sel(TT));
  Multiplexer #(.select(1), .width(5), .disabled("Z"), .enable("false")) multiplexer_7 (
    .in0(5'b00001), .in1(5'b10000), .out(multiplexer_7_out), .sel(AM_FM));
  Multiplexer #(.select(1), .width(5), .disabled("Z"), .enable("false")) multiplexer_8 (
    .in0({5{1'b0}}), .in1(multiplexer_7_out), .out(out_6), .sel(TT));
endmodule

module \上下午文字显示测试电路  (
  input  in_1,
  input  in_2
);

  wire [4:0] \上下午文字显示的电路_1_out_3 , \上下午文字显示的电路_1_out_4 , \上下午文字显示的电路_1_out_5 , \上下午文字显示的电路_1_out_6 ;

  \上下午文字显示的电路  \u_上下午文字显示的电路_1  (
    .AM_FM(in_1), .TT(in_2), .out_3(\上下午文字显示的电路_1_out_3 ), .out_4(\上下午文字显示的电路_1_out_4 ),
    .out_5(\上下午文字显示的电路_1_out_5 ), .out_6(\上下午文字显示的电路_1_out_6 ));
  DotMatrix #(.inputtype("column"), .matrixcols(4), .matrixrows(5), .persist(0), .dotshape("square")) dotmatrix_1 (
    .col0(\上下午文字显示的电路_1_out_3 ), .col1(\上下午文字显示的电路_1_out_4 ), .col2(\上下午文字显示的电路_1_out_5 ),
    .col3(\上下午文字显示的电路_1_out_6 ));
endmodule

module \电子钟整点报时电路  (
  input  [3:0] \分钟十位 ,
  input  [3:0] \分钟个位 ,
  input  [3:0] \秒钟十位 ,
  output LED
);

  wire and_1_out, and_2_out, and_3_out;
  wire [3:0] xnor_1_out, xnor_2_out, xnor_3_out;

  assign xnor_1_out = ~(\分钟十位  ^ 4'b0101);  // XNOR_Gate xnor_1, 4 bits wide
  assign xnor_2_out = ~(\分钟个位  ^ 4'b1001);  // XNOR_Gate xnor_2, 4 bits wide
  assign xnor_3_out = ~(\秒钟十位  ^ 4'b0101);  // XNOR_Gate xnor_3, 4 bits wide
  and and_1 (and_1_out, xnor_1_out[0], xnor_1_out[1], xnor_1_out[2], xnor_1_out[3]);
  and and_2 (and_2_out, xnor_2_out[0], xnor_2_out[1], xnor_2_out[2], xnor_2_out[3]);
  and and_3 (and_3_out, xnor_3_out[0], xnor_3_out[1], xnor_3_out[2], xnor_3_out[3]);
  and and_4 (LED, and_1_out, and_2_out, and_3_out);
endmodule

module \电子钟整点报时电路测试电路  (
  input  in_1,
  input  in_2
);

  wire button_1_out, button_2_out, button_3_out, button_4_out, clock_1_out, \六十进制计数器_1_nqcc进位 ,
       \电子钟整点报时电路_1_led ;
  wire [3:0] \六十进制计数器_1_out_9 , \六十进制计数器_1_out_13 , \六十进制计数器_2_out_9 , \六十进制计数器_2_out_13 ;

  Clock #(.highDuration(1), .lowDuration(1)) clock_1 (.out(clock_1_out));
  Button button_1 (.out(button_1_out));
  Hex_Digit_Display hex_digit_display_1 (.value(\六十进制计数器_1_out_13 ), .dp(1'b0));
  Hex_Digit_Display hex_digit_display_2 (.value(\六十进制计数器_1_out_9 ), .dp(1'b0));
  \六十进制计数器  \u_六十进制计数器_1  (
    .CPU(clock_1_out), .CPD(button_1_out), .ADJ(in_1), .\nQcc进位 (\六十进制计数器_1_nqcc进位 ),
    .out_6(\六十进制计数器_1_out_9 [3]), .out_7(\六十进制计数器_1_out_9 [2]), .out_8(\六十进制计数器_1_out_9 [1]),
    .out_9(\六十进制计数器_1_out_9 [0]), .out_10(\六十进制计数器_1_out_13 [3]), .out_11(\六十进制计数器_1_out_13 [2]),
    .out_12(\六十进制计数器_1_out_13 [1]), .out_13(\六十进制计数器_1_out_13 [0]), .CLR(button_2_out));
  \电子钟整点报时电路  \u_电子钟整点报时电路_1  (
    .\分钟十位 (\六十进制计数器_2_out_13 ), .\分钟个位 (\六十进制计数器_2_out_9 ), .\秒钟十位 (\六十进制计数器_1_out_13 ),
    .LED(\电子钟整点报时电路_1_led ));
  Button button_2 (.out(button_2_out));
  LED #(.active("true")) led_1 (.in(\电子钟整点报时电路_1_led ));
  Button button_3 (.out(button_3_out));
  Hex_Digit_Display hex_digit_display_3 (.value(\六十进制计数器_2_out_13 ), .dp(1'b0));
  Hex_Digit_Display hex_digit_display_4 (.value(\六十进制计数器_2_out_9 ), .dp(1'b0));
  \六十进制计数器  \u_六十进制计数器_2  (
    .CPU(\六十进制计数器_1_nqcc进位 ), .CPD(button_3_out), .ADJ(in_2), .out_6(\六十进制计数器_2_out_9 [3]),
    .out_7(\六十进制计数器_2_out_9 [2]), .out_8(\六十进制计数器_2_out_9 [1]), .out_9(\六十进制计数器_2_out_9 [0]),
    .out_10(\六十进制计数器_2_out_13 [3]), .out_11(\六十进制计数器_2_out_13 [2]), .out_12(\六十进制计数器_2_out_13 [1]),
    .out_13(\六十进制计数器_2_out_13 [0]), .CLR(button_4_out));  // open: nQcc进位
  Button button_4 (.out(button_4_out));

  // Notes on the sheet:
  //   秒
  //   分
endmodule

module \秒脉冲产生电路  (
  input  in_1,
  output out_2
);

  wire and_2_out, and_3_out, buffer_1_out, buffer_2_out, not_1_out, not_2_out, not_3_out, or_1_out,
       \四位二进制可逆计数器_1_p2 , \四位二进制可逆计数器_1_p4 , \四位二进制可逆计数器_1_p7 , \四位二进制可逆计数器_1_p9 , \四位二进制可逆计数器_1_p11 ;

  // 实验5_CSXJ1901_U201912703_时深奥_四位二进制可逆计数器 四位二进制可逆计数器_1: pin names not known; wires that end beside it: in_1, \四位二进制可逆计数器_1_p2 , 1'b0, \四位二进制可逆计数器_1_p4 , 1'b0, 1'b0, \四位二进制可逆计数器_1_p7 , 1'b0, \四位二进制可逆计数器_1_p9 , 1'b0, \四位二进制可逆计数器_1_p11 , 1'b1
  and and_1 (\四位二进制可逆计数器_1_p2 , and_2_out, and_3_out);
  and and_2 (and_2_out, buffer_1_out, not_1_out);
  buf buffer_1 (buffer_1_out, \四位二进制可逆计数器_1_p4 );
  not not_1 (not_1_out, \四位二进制可逆计数器_1_p7 );
  or or_1 (or_1_out, in_1, buffer_2_out);
  buf buffer_2 (buffer_2_out, \四位二进制可逆计数器_1_p2 );
  and and_3 (and_3_out, not_3_out, not_2_out);
  not not_2 (not_2_out, \四位二进制可逆计数器_1_p11 );
  not not_3 (not_3_out, \四位二进制可逆计数器_1_p9 );
  J_K_Flip_Flop #(.trigger("rising"), .Pre_Clr_Positions("ABOVE_BELOW"), .NegatePresetClear("false"), .enable("false"), .NewFFLayout("true")) j_k_ff_1 (
    .J(\四位二进制可逆计数器_1_p2 ), .clk(or_1_out), .K(1'b1), .Q(out_2));  // open: Qn, preset, reset
endmodule

module \闹钟  (
  input  [3:0] \时钟小时十位 ,
  input  [3:0] \设定小时十位 ,
  input  [3:0] \时钟小时个位 ,
  input  [3:0] \设定小时个位 ,
  input  [3:0] \时钟分钟十位 ,
  input  \开关 ,
  input  [3:0] \设定分钟十位 ,
  input  [3:0] \时钟分钟个位 ,
  input  [3:0] \设定分钟个位 ,
  input  [3:0] \时钟秒钟十位 ,
  output [3:0] out_11,
  output [3:0] out_12,
  output LED,
  output [3:0] out_14,
  output [3:0] out_15
);

  wire and_1_out, and_2_out, and_3_out, and_5_out, and_6_out;
  wire [3:0] xnor_1_out, xnor_2_out, xnor_3_out, xnor_4_out, xnor_5_out;

  assign xnor_1_out = ~(\时钟小时十位  ^ \设定小时十位 );  // XNOR_Gate xnor_1, 4 bits wide
  assign xnor_2_out = ~(\时钟小时个位  ^ \设定小时个位 );  // XNOR_Gate xnor_2, 4 bits wide
  assign xnor_3_out = ~(\时钟分钟十位  ^ \设定分钟十位 );  // XNOR_Gate xnor_3, 4 bits wide
  assign xnor_4_out = ~(\时钟分钟个位  ^ \设定分钟个位 );  // XNOR_Gate xnor_4, 4 bits wide
  assign xnor_5_out = ~(\时钟秒钟十位  ^ 4'b0000);  // XNOR_Gate xnor_5, 4 bits wide
  and and_1 (and_1_out, xnor_1_out[0], xnor_1_out[1], xnor_1_out[2], xnor_1_out[3]);
  and and_2 (and_2_out, xnor_2_out[0], xnor_2_out[1], xnor_2_out[2], xnor_2_out[3]);
  and and_3 (and_3_out, xnor_3_out[0], xnor_3_out[1], xnor_3_out[2], xnor_3_out[3]);
  and and_4 (and_3_out, xnor_4_out[0], xnor_4_out[1], xnor_4_out[2], xnor_4_out[3]);
  and and_5 (and_5_out, xnor_5_out[0], xnor_5_out[1], xnor_5_out[2], xnor_5_out[3]);
  and and_6 (and_6_out, and_1_out, and_2_out, and_3_out, and_3_out, and_5_out);
  and and_7 (LED, and_6_out, \开关 );

  assign out_11 = \设定小时十位 ;
  assign out_12 = \设定小时个位 ;
  assign out_14 = \设定分钟十位 ;
  assign out_15 = \设定分钟个位 ;
endmodule

module \闹钟测试  (
  input  [3:0] in_1,
  input  [3:0] in_2,
  input  [3:0] in_3,
  input  [3:0] in_4,
  input  in_5,
  input  in_6,
  input  in_7,
  input  in_8,
  input  in_9,
  output out_10
);

  wire button_1_out, button_2_out, button_3_out, button_4_out, button_5_out, button_6_out, clock_1_out,
       \六十进制计数器_1_nqcc进位 , \六十进制计数器_2_nqcc进位 , \闹钟_1_led ;
  wire [3:0] \六十进制计数器_1_out_9 , \六十进制计数器_1_out_13 , \六十进制计数器_2_out_9 , \六十进制计数器_2_out_13 ,
       \十二进制计数器或二十四进制的计数器电路_1__24进制进位 , \十二进制计数器或二十四进制的计数器电路_1_out_9 , \闹钟_1_out_11 , \闹钟_1_out_12 ,
       \闹钟_1_out_14 , \闹钟_1_out_15 ;

  Clock #(.highDuration(1), .lowDuration(1)) clock_1 (.out(clock_1_out));
  Button button_1 (.out(button_1_out));
  Hex_Digit_Display hex_digit_display_1 (.value(\六十进制计数器_1_out_13 ), .dp(1'b0));
  Hex_Digit_Display hex_digit_display_2 (.value(\六十进制计数器_1_out_9 ), .dp(1'b0));
  \六十进制计数器  \u_六十进制计数器_1  (
    .CPU(clock_1_out), .CPD(button_1_out), .ADJ(in_6), .\nQcc进位 (\六十进制计数器_1_nqcc进位 ),
    .out_6(\六十进制计数器_1_out_9 [3]), .out_7(\六十进制计数器_1_out_9 [2]), .out_8(\六十进制计数器_1_out_9 [1]),
    .out_9(\六十进制计数器_1_out_9 [0]), .out_10(\六十进制计数器_1_out_13 [3]), .out_11(\六十进制计数器_1_out_13 [2]),
    .out_12(\六十进制计数器_1_out_13 [1]), .out_13(\六十进制计数器_1_out_13 [0]), .CLR(button_2_out));
  Button button_2 (.out(button_2_out));
  Button button_3 (.out(button_3_out));
  Hex_Digit_Display hex_digit_display_3 (.value(\六十进制计数器_2_out_13 ), .dp(1'b0));
  Hex_Digit_Display hex_digit_display_4 (.value(\六十进制计数器_2_out_9 ), .dp(1'b0));
  \六十进制计数器  \u_六十进制计数器_2  (
    .CPU(\六十进制计数器_1_nqcc进位 ), .CPD(button_3_out), .ADJ(in_7), .\nQcc进位 (\六十进制计数器_2_nqcc进位 ),
    .out_6(\六十进制计数器_2_out_9 [3]), .out_7(\六十进制计数器_2_out_9 [2]), .out_8(\六十进制计数器_2_out_9 [1]),
    .out_9(\六十进制计数器_2_out_9 [0]), .out_10(\六十进制计数器_2_out_13 [3]), .out_11(\六十进制计数器_2_out_13 [2]),
    .out_12(\六十进制计数器_2_out_13 [1]), .out_13(\六十进制计数器_2_out_13 [0]), .CLR(button_4_out));
  Button button_4 (.out(button_4_out));
  Button button_5 (.out(button_5_out));
  Hex_Digit_Display hex_digit_display_5 (.value(\十二进制计数器或二十四进制的计数器电路_1_out_9 ), .dp(1'b0));
  Hex_Digit_Display hex_digit_display_6 (.value(\十二进制计数器或二十四进制的计数器电路_1__24进制进位 ), .dp(1'b0));
  \十二进制计数器或二十四进制的计数器电路  \u_十二进制计数器或二十四进制的计数器电路_1  (
    .CPu(\六十进制计数器_2_nqcc进位 ), .ADJ(in_8), .CPd(button_5_out), .\nQcc_进位 (out_10), .CLR(button_6_out),
    .out_6(\十二进制计数器或二十四进制的计数器电路_1_out_9 [3]), .out_7(\十二进制计数器或二十四进制的计数器电路_1_out_9 [2]),
    .out_8(\十二进制计数器或二十四进制的计数器电路_1_out_9 [1]), .out_9(\十二进制计数器或二十四进制的计数器电路_1_out_9 [0]),
    .out_10(\十二进制计数器或二十四进制的计数器电路_1__24进制进位 [3]), .out_11(\十二进制计数器或二十四进制的计数器电路_1__24进制进位 [2]),
    .out_12(\十二进制计数器或二十四进制的计数器电路_1__24进制进位 [1]), .\_24进制进位 (\十二进制计数器或二十四进制的计数器电路_1__24进制进位 [0]), .SET(in_9));
  Button button_6 (.out(button_6_out));
  \闹钟  \u_闹钟_1  (
    .\时钟小时十位 (\十二进制计数器或二十四进制的计数器电路_1_out_9 ), .\设定小时十位 (in_1), .\时钟小时个位 (\十二进制计数器或二十四进制的计数器电路_1__24进制进位 ),
    .\设定小时个位 (in_2), .\时钟分钟十位 (\六十进制计数器_2_out_13 ), .\开关 (in_5), .\设定分钟十位 (in_3),
    .\时钟分钟个位 (\六十进制计数器_2_out_9 ), .\设定分钟个位 (in_4), .\时钟秒钟十位 (\六十进制计数器_1_out_13 ), .out_11(\闹钟_1_out_11 ),
    .out_12(\闹钟_1_out_12 ), .LED(\闹钟_1_led ), .out_14(\闹钟_1_out_14 ), .out_15(\闹钟_1_out_15 ));
  Hex_Digit_Display hex_digit_display_7 (.value(\闹钟_1_out_11 ), .dp(1'b0));
  Hex_Digit_Display hex_digit_display_8 (.value(\闹钟_1_out_12 ), .dp(1'b0));
  LED #(.active("true")) led_1 (.in(\闹钟_1_led ));
  Hex_Digit_Display hex_digit_display_9 (.value(\闹钟_1_out_14 ), .dp(1'b0));
  Hex_Digit_Display hex_digit_display_10 (.value(\闹钟_1_out_15 ), .dp(1'b0));

  // Notes on the sheet:
  //   秒
  //   分
  //   时
endmodule

module \多功能数字钟  (
  input  [3:0] in_1,
  input  [3:0] in_2,
  input  [3:0] in_3,
  input  [3:0] in_4,
  input  in_5,
  input  CPu,
  input  _8Hz,
  input  SET,
  input  CPd,
  input  ADj0,
  input  ADj1,
  input  CLR,
  output \闹钟判断 ,
  output [4:0] out_14,
  output [4:0] out_15,
  output [4:0] out_16,
  output [4:0] out_17,
  output \整点判断 ,
  output [3:0] \时钟十位 ,
  output [3:0] \时钟个位 ,
  output [3:0] \分钟十位 ,
  output [3:0] \分钟个位 ,
  output [3:0] \秒钟十位 ,
  output [3:0] \秒钟个位 
);

  wire and_1_out, and_2_out, and_3_out, and_4_out, and_5_out, and_6_out, and_7_out, and_8_out, and_10_out,
       comparator_1_lt, comparator_2_lt, d_ff_1_q, d_ff_1_qn, not_1_out, not_2_out, not_3_out, not_4_out,
       not_5_out, not_6_out, not_7_out, or_1_out, or_2_out, or_3_out, or_4_out, \六十进制计数器_1_nqcc进位 ,
       \六十进制计数器_2_nqcc进位 , \十二进制计数器或二十四进制的计数器电路_1_nqcc_进位 , \秒脉冲产生电路_1_out_2 ;
  wire [0:0] and_9_out;
  wire [3:0] multiplexer_2_out, multiplexer_4_out, multiplexer_5_out, subtractor_1_out,
       \先行进位并行加法器测试电路_1_p10 , \十二进制计数器或二十四进制的计数器电路_1__24进制进位 , \十二进制计数器或二十四进制的计数器电路_1_out_9 ;

  \秒脉冲产生电路  \u_秒脉冲产生电路_1  (.in_1(_8Hz), .out_2(\秒脉冲产生电路_1_out_2 ));
  \六十进制计数器  \u_六十进制计数器_1  (
    .CPU(\秒脉冲产生电路_1_out_2 ), .CPD(1'b0), .ADJ(1'b0), .\nQcc进位 (\六十进制计数器_1_nqcc进位 ), .out_6(\秒钟个位 [3]),
    .out_7(\秒钟个位 [2]), .out_8(\秒钟个位 [1]), .out_9(\秒钟个位 [0]), .out_10(\秒钟十位 [3]), .out_11(\秒钟十位 [2]),
    .out_12(\秒钟十位 [1]), .out_13(\秒钟十位 [0]), .CLR(CLR));
  \电子钟整点报时电路  \u_电子钟整点报时电路_1  (.\分钟十位 (\分钟十位 ), .\分钟个位 (\分钟个位 ), .\秒钟十位 (\秒钟十位 ), .LED(\整点判断 ));
  and and_1 (and_1_out, \六十进制计数器_1_nqcc进位 , not_1_out);
  not not_1 (not_1_out, ADj0);
  and and_2 (and_2_out, ADj0, not_2_out);
  not not_2 (not_2_out, ADj1);
  and and_3 (and_3_out, and_2_out, CPu);
  or or_1 (or_1_out, and_3_out, and_1_out);
  \六十进制计数器  \u_六十进制计数器_2  (
    .CPU(or_1_out), .CPD(CPd), .ADJ(and_2_out), .\nQcc进位 (\六十进制计数器_2_nqcc进位 ), .out_6(\分钟个位 [3]),
    .out_7(\分钟个位 [2]), .out_8(\分钟个位 [1]), .out_9(\分钟个位 [0]), .out_10(\分钟十位 [3]), .out_11(\分钟十位 [2]),
    .out_12(\分钟十位 [1]), .out_13(\分钟十位 [0]), .CLR(CLR));
  and and_4 (and_4_out, CPu, and_6_out);
  or or_2 (or_2_out, and_4_out, and_5_out);
  and and_5 (and_5_out, not_1_out, \六十进制计数器_2_nqcc进位 );
  and and_6 (and_6_out, ADj0, ADj1);
  Multiplexer #(.select(1), .width(4), .disabled("Z"), .enable("false")) multiplexer_1 (
    .in0(multiplexer_2_out), .in1(\十二进制计数器或二十四进制的计数器电路_1_out_9 ), .out(\时钟十位 ), .sel(SET));
  and and_7 (and_7_out, \十二进制计数器或二十四进制的计数器电路_1_out_9 [0], not_6_out);
  or or_3 (or_3_out, and_7_out, and_8_out);
  and and_8 (and_8_out, not_4_out, \十二进制计数器或二十四进制的计数器电路_1_out_9 [1]);
  Multiplexer #(.select(1), .width(4), .disabled("Z"), .enable("false")) multiplexer_2 (
    .in0(\十二进制计数器或二十四进制的计数器电路_1_out_9 ), .in1({\十二进制计数器或二十四进制的计数器电路_1_out_9 [3:2], 1'b0, and_9_out[0]}),
    .out(multiplexer_2_out), .sel(or_3_out));
  not not_3 (not_3_out, \十二进制计数器或二十四进制的计数器电路_1_out_9 [0]);
  and and_9 (and_9_out[0], not_3_out, and_10_out);
  and and_10 (and_10_out, and_8_out, not_5_out);
  \闹钟  \u_闹钟_1  (
    .\时钟小时十位 (\时钟十位 ), .\设定小时十位 (in_1), .\时钟小时个位 (\时钟个位 ), .\设定小时个位 (in_2), .\时钟分钟十位 (\分钟十位 ), .\开关 (in_5),
    .\设定分钟十位 (in_3), .\时钟分钟个位 (\分钟个位 ), .\设定分钟个位 (in_4), .\时钟秒钟十位 (\秒钟十位 ), .LED(\闹钟判断 ));  // open: out_11, out_12, out_14, out_15
  Multiplexer #(.select(1), .width(4), .disabled("Z"), .enable("false")) multiplexer_3 (
    .in0(multiplexer_4_out), .in1(\十二进制计数器或二十四进制的计数器电路_1__24进制进位 ), .out(\时钟个位 ), .sel(SET));
  \十二进制计数器或二十四进制的计数器电路  \u_十二进制计数器或二十四进制的计数器电路_1  (
    .CPu(or_2_out), .ADJ(and_6_out), .CPd(CPd), .\nQcc_进位 (\十二进制计数器或二十四进制的计数器电路_1_nqcc_进位 ), .CLR(CLR),
    .out_6(\十二进制计数器或二十四进制的计数器电路_1_out_9 [3]), .out_7(\十二进制计数器或二十四进制的计数器电路_1_out_9 [2]),
    .out_8(\十二进制计数器或二十四进制的计数器电路_1_out_9 [1]), .out_9(\十二进制计数器或二十四进制的计数器电路_1_out_9 [0]),
    .out_10(\十二进制计数器或二十四进制的计数器电路_1__24进制进位 [3]), .out_11(\十二进制计数器或二十四进制的计数器电路_1__24进制进位 [2]),
    .out_12(\十二进制计数器或二十四进制的计数器电路_1__24进制进位 [1]), .\_24进制进位 (\十二进制计数器或二十四进制的计数器电路_1__24进制进位 [0]), .SET(1'b1));
  not not_4 (not_4_out, \十二进制计数器或二十四进制的计数器电路_1_out_9 [0]);
  Multiplexer #(.select(1), .width(4), .disabled("Z"), .enable("false")) multiplexer_4 (
    .in0(\十二进制计数器或二十四进制的计数器电路_1__24进制进位 ), .in1(subtractor_1_out), .out(multiplexer_4_out), .sel(or_3_out));
  // Probe on \十二进制计数器或二十四进制的计数器电路_1__24进制进位 
  not not_5 (not_5_out, comparator_2_lt);
  or or_4 (or_4_out, \十二进制计数器或二十四进制的计数器电路_1_nqcc_进位 , and_7_out);
  Comparator #(.width(4), .mode("unsigned")) comparator_1 (
    .a(\十二进制计数器或二十四进制的计数器电路_1__24进制进位 ), .b(4'b0010), .lt(comparator_1_lt));  // open: gt, eq
  not not_6 (not_6_out, comparator_1_lt);
  Comparator #(.width(4), .mode("unsigned")) comparator_2 (
    .a(\十二进制计数器或二十四进制的计数器电路_1__24进制进位 ), .b(4'b0010), .lt(comparator_2_lt));  // open: gt, eq
  // 先行进位并行加法器测试电路 先行进位并行加法器测试电路_1: pin names not known; wires that end beside it: \十二进制计数器或二十四进制的计数器电路_1__24进制进位 [0], \十二进制计数器或二十四进制的计数器电路_1__24进制进位 [1], \十二进制计数器或二十四进制的计数器电路_1__24进制进位 [2], \十二进制计数器或二十四进制的计数器电路_1__24进制进位 [3], 1'b1, 1'b0, 1'b1, 1'b0, 1'b0, \先行进位并行加法器测试电路_1_p10 [0], \先行进位并行加法器测试电路_1_p10 [1], \先行进位并行加法器测试电路_1_p10 [2], \先行进位并行加法器测试电路_1_p10 [3]
  D_Flip_Flop #(.trigger("rising"), .Pre_Clr_Positions("ABOVE_BELOW"), .NegatePresetClear("false"), .enable("false"), .NewFFLayout("true")) d_ff_1 (
    .clk(or_4_out), .D(d_ff_1_qn), .Q(d_ff_1_q), .Qn(d_ff_1_qn), .preset(1'b0), .reset(CLR));
  Multiplexer #(.select(1), .width(4), .disabled("Z"), .enable("false")) multiplexer_5 (
    .in0(\十二进制计数器或二十四进制的计数器电路_1__24进制进位 ), .in1(\先行进位并行加法器测试电路_1_p10 ), .out(multiplexer_5_out),
    .sel(comparator_2_lt));
  \上下午文字显示的电路  \u_上下午文字显示的电路_1  (
    .AM_FM(d_ff_1_q), .TT(not_7_out), .out_3(out_14), .out_4(out_15), .out_5(out_16), .out_6(out_17));
  not not_7 (not_7_out, SET);
  // Probe on subtractor_1_out
  Subtractor #(.width(4)) subtractor_1 (.a(multiplexer_5_out), .b(4'b0010), .out(subtractor_1_out));  // open: bin, bout
  // Probe on \先行进位并行加法器测试电路_1_p10 

  // Notes on the sheet:
  //   秒
  //   分
  //   12<=H<20
  //   H>=20
  //   时
endmodule

module \多功能数字钟测试电路  (
  input  in_1,
  input  in_2,
  input  in_3,
  input  in_4,
  input  [3:0] \时十 ,
  input  [3:0] \时个 ,
  input  [3:0] \分十 ,
  input  [3:0] \分个 
);

  wire button_1_out, button_2_out, button_3_out, clock_1_out, \多功能数字钟_1_整点判断 , \多功能数字钟_1_闹钟判断 ;
  wire [3:0] \多功能数字钟_1_分钟个位 , \多功能数字钟_1_分钟十位 , \多功能数字钟_1_时钟个位 , \多功能数字钟_1_时钟十位 , \多功能数字钟_1_秒钟个位 ,
       \多功能数字钟_1_秒钟十位 ;
  wire [4:0] \多功能数字钟_1_out_14 , \多功能数字钟_1_out_15 , \多功能数字钟_1_out_16 , \多功能数字钟_1_out_17 ;

  DotMatrix #(.inputtype("column"), .matrixcols(4), .matrixrows(5), .persist(0), .dotshape("square")) dotmatrix_1 (
    .col0(\多功能数字钟_1_out_14 ), .col1(\多功能数字钟_1_out_15 ), .col2(\多功能数字钟_1_out_16 ), .col3(\多功能数字钟_1_out_17 ));
  Clock #(.highDuration(1), .lowDuration(1)) clock_1 (.out(clock_1_out));
  Button button_1 (.out(button_1_out));
  Button button_2 (.out(button_2_out));
  Hex_Digit_Display hex_digit_display_1 (.value(\多功能数字钟_1_时钟个位 ), .dp(1'b1));
  Hex_Digit_Display hex_digit_display_2 (.value(\多功能数字钟_1_时钟十位 ), .dp(1'b0));
  Button button_3 (.out(button_3_out));
  Hex_Digit_Display hex_digit_display_3 (.value(\多功能数字钟_1_分钟个位 ), .dp(1'b1));
  Hex_Digit_Display hex_digit_display_4 (.value(\多功能数字钟_1_分钟十位 ), .dp(1'b0));
  \多功能数字钟  \u_多功能数字钟_1  (
    ._8Hz(clock_1_out), .CPd(button_1_out), .in_1(\时十 ), .in_2(\时个 ), .in_3(\分十 ), .in_4(\分个 ), .in_5(in_3),
    .SET(in_4), .\秒钟十位 (\多功能数字钟_1_秒钟十位 ), .\秒钟个位 (\多功能数字钟_1_秒钟个位 ), .\整点判断 (\多功能数字钟_1_整点判断 ),
    .\分钟十位 (\多功能数字钟_1_分钟十位 ), .\分钟个位 (\多功能数字钟_1_分钟个位 ), .\时钟十位 (\多功能数字钟_1_时钟十位 ), .\时钟个位 (\多功能数字钟_1_时钟个位 ),
    .\闹钟判断 (\多功能数字钟_1_闹钟判断 ), .out_14(\多功能数字钟_1_out_14 ), .out_15(\多功能数字钟_1_out_15 ),
    .out_16(\多功能数字钟_1_out_16 ), .out_17(\多功能数字钟_1_out_17 ), .CLR(button_3_out), .ADj0(in_1), .ADj1(in_2),
    .CPu(button_2_out));
  LED #(.active("true")) led_1 (.in(\多功能数字钟_1_闹钟判断 ));
  LED #(.active("true")) led_2 (.in(\多功能数字钟_1_整点判断 ));
  Hex_Digit_Display hex_digit_display_5 (.value(\多功能数字钟_1_秒钟个位 ), .dp(1'b0));
  Hex_Digit_Display hex_digit_display_6 (.value(\多功能数字钟_1_秒钟十位 ), .dp(1'b0));
  Hex_Digit_Display hex_digit_display_7 (.value(\时十 ), .dp(1'b0));
  Hex_Digit_Display hex_digit_display_8 (.value(\时个 ), .dp(1'b1));
  Hex_Digit_Display hex_digit_display_9 (.value(\分十 ), .dp(1'b0));
  Hex_Digit_Display hex_digit_display_10 (.value(\分个 ), .dp(1'b0));
endmodule
