// Logisim project 6 斐波那契数列.circ as structural Verilog: 7 circuits, main circuit sqrX
module sqrX (
  input  [31:0] A,
  input  [31:0] B,
  input  [31:0] C,
  input  [31:0] D,
  output [31:0] A_prime,
  output [31:0] B_prime,
  output [31:0] C_prime,
  output [31:0] D_prime
);

  wire [31:0] multiplier_1_out, multiplier_2_out, multiplier_3_out, multiplier_4_out, multiplier_5_out,
       multiplier_6_out, multiplier_7_out;

  Multiplier #(.width(32)) multiplier_1 (.a(A), .b(A), .out(multiplier_1_out), .cin({32{1'b0}}));  // open: cout
  Multiplier #(.width(32)) multiplier_2 (.a(A), .b(B), .out(multiplier_2_out), .cin({32{1'b0}}));  // open: cout
  Multiplier #(.width(32)) multiplier_3 (.a(B), .b(C), .out(multiplier_3_out), .cin({32{1'b0}}));  // open: cout
  Multiplier #(.width(32)) multiplier_4 (.a(A), .b(C), .out(multiplier_4_out), .cin({32{1'b0}}));  // open: cout
  Multiplier #(.width(32)) multiplier_5 (.a(C), .b(D), .out(multiplier_5_out), .cin({32{1'b0}}));  // open: cout
  Multiplier #(.width(32)) multiplier_6 (.a(D), .b(D), .out(multiplier_6_out), .cin({32{1'b0}}));  // open: cout
  Multiplier #(.width(32)) multiplier_7 (.a(B), .b(D), .out(multiplier_7_out));  // open: cin, cout
  Adder #(.width(32)) adder_1 (.a(multiplier_1_out), .b(multiplier_3_out), .out(A_prime));  // open: cin, cout
  Adder #(.width(32)) adder_2 (.a(multiplier_2_out), .b(multiplier_7_out), .out(B_prime), .cin(1'b0));  // open: cout
  Adder #(.width(32)) adder_3 (.a(multiplier_4_out), .b(multiplier_5_out), .out(C_prime), .cin(1'b0));  // open: cout
  Adder #(.width(32)) adder_4 (.a(multiplier_3_out), .b(multiplier_6_out), .out(D_prime), .cin(1'b0));  // open: cout

  // Notes on the sheet:
  //   a^2
  //   ab
  //   bc
  //   ac
  //   cd
  //   d^2
  //   bd
endmodule

module sqrX_A (
  input  [31:0] A,
  input  [31:0] B,
  input  [31:0] C,
  input  [31:0] D,
  output [31:0] A_prime,
  output [31:0] B_prime,
  output [31:0] C_prime,
  output [31:0] D_prime
);

  wire [31:0] sqrx_1_a_prime, sqrx_1_c_prime;

  sqrX sqrx_1 (
    .A(A), .B(B), .C(C), .D(D), .A_prime(sqrx_1_a_prime), .B_prime(A_prime), .C_prime(sqrx_1_c_prime),
    .D_prime(C_prime));
  Adder #(.width(32)) adder_1 (.a(sqrx_1_a_prime), .b(A_prime), .out(B_prime));  // open: cin, cout
  Adder #(.width(32)) adder_2 (.a(sqrx_1_c_prime), .b(C_prime), .out(D_prime));  // open: cin, cout
endmodule

module \矩阵快速幂算法迭代  (
  input  Start,
  input  Ni_1,
  input  Clock,
  input  Clear,
  output [31:0] Fi
);

  wire [31:0] multiplexer_1_out, multiplexer_2_out, multiplexer_3_out, multiplexer_4_out, multiplexer_5_out,
       multiplexer_6_out, multiplexer_7_out, multiplexer_8_out, register_1_q, register_3_q, register_4_q,
       sqrx_1_a_prime, sqrx_1_b_prime, sqrx_1_c_prime, sqrx_1_d_prime, sqrx_a_1_a_prime, sqrx_a_1_b_prime,
       sqrx_a_1_c_prime, sqrx_a_1_d_prime;

  Multiplexer #(.select(1), .width(32), .disabled("Z"), .enable("false")) multiplexer_1 (
    .in0({32{1'b0}}), .in1(multiplexer_5_out), .out(multiplexer_1_out), .sel(Start));
  Register #(.width(32), .trigger("rising"), .Select("low")) register_1 (
    .D(multiplexer_1_out), .en(1'b1), .Q(register_1_q), .clk(Clock), .clr(Clear), .cs(1'b0), .preset(1'b0));
  Multiplexer #(.select(1), .width(32), .disabled("Z"), .enable("false")) multiplexer_2 (
    .in0(32'h1), .in1(multiplexer_6_out), .out(multiplexer_2_out), .sel(Start));
  Register #(.width(32), .trigger("rising"), .Select("low")) register_2 (
    .D(multiplexer_2_out), .en(1'b1), .Q(Fi), .clk(Clock), .clr(Clear), .cs(1'b0), .preset(1'b0));
  Multiplexer #(.select(1), .width(32), .disabled("Z"), .enable("false")) multiplexer_3 (
    .in0(32'h1), .in1(multiplexer_7_out), .out(multiplexer_3_out), .sel(Start));
  Register #(.width(32), .trigger("rising"), .Select("low")) register_3 (
    .D(multiplexer_3_out), .en(1'b1), .Q(register_3_q), .clk(Clock), .clr(Clear), .cs(1'b0), .preset(1'b0));
  Register #(.width(32), .trigger("rising"), .Select("low")) register_4 (
    .D(multiplexer_4_out), .en(1'b1), .Q(register_4_q), .clk(Clock), .clr(Clear), .cs(1'b0), .preset(1'b0));
  Multiplexer #(.select(1), .width(32), .disabled("Z"), .enable("false")) multiplexer_4 (
    .in0(32'h1), .in1(multiplexer_8_out), .out(multiplexer_4_out), .sel(Start));
  sqrX sqrx_1 (
    .A(register_1_q), .B(Fi), .C(register_3_q), .D(register_4_q), .A_prime(sqrx_1_a_prime),
    .B_prime(sqrx_1_b_prime), .C_prime(sqrx_1_c_prime), .D_prime(sqrx_1_d_prime));
  sqrX_A sqrx_a_1 (
    .A(register_1_q), .B(Fi), .C(register_3_q), .D(register_4_q), .A_prime(sqrx_a_1_a_prime),
    .B_prime(sqrx_a_1_b_prime), .C_prime(sqrx_a_1_c_prime), .D_prime(sqrx_a_1_d_prime));
  Multiplexer #(.select(1), .width(32), .disabled("Z"), .enable("false")) multiplexer_5 (
    .in0(sqrx_1_a_prime), .in1(sqrx_a_1_a_prime), .out(multiplexer_5_out), .sel(Ni_1));
  Multiplexer #(.select(1), .width(32), .disabled("Z"), .enable("false")) multiplexer_6 (
    .in0(sqrx_1_b_prime), .in1(sqrx_a_1_b_prime), .out(multiplexer_6_out), .sel(Ni_1));
  Multiplexer #(.select(1), .width(32), .disabled("Z"), .enable("false")) multiplexer_7 (
    .in0(sqrx_1_c_prime), .in1(sqrx_a_1_c_prime), .out(multiplexer_7_out), .sel(Ni_1));
  Multiplexer #(.select(1), .width(32), .disabled("Z"), .enable("false")) multiplexer_8 (
    .in0(sqrx_1_d_prime), .in1(sqrx_a_1_d_prime), .out(multiplexer_8_out), .sel(Ni_1));
endmodule

module \控制器  (
  input  [5:0] n,
  input  Clock,
  input  Clear,
  output Ni_1,
  output Start,
  output Clock_2,
  output Clear_2
);

  wire comparator_1_lt, or_1_out, or_2_out;
  wire [7:0] counter_1_q;

  Comparator #(.width(8), .mode("unsigned")) comparator_1 (
    .a(counter_1_q), .b(8'h6), .lt(comparator_1_lt));  // open: gt, eq
  Shift_Register #(.width(1), .length(6), .parallel("true"), .trigger("rising")) shift_register_1 (
    .shift(1'b1), .clk(or_1_out), .out(Ni_1), .load(Clear), .clr(1'b0), .d0(n[0]), .d1(n[1]), .d2(n[2]),
    .d3(n[3]), .d4(n[4]), .d5(n[5]));  // open: in, q0, q1, q2, q3, q4, q5
  or or_1 (or_1_out, Clear, Clock);
  and and_1 (Clock_2, Clock, comparator_1_lt);
  or or_2 (or_2_out, Ni_1, Start);
  D_Flip_Flop #(.trigger("rising"), .Pre_Clr_Positions("ABOVE_BELOW"), .NegatePresetClear("false"), .enable("false"), .NewFFLayout("true")) d_ff_1 (
    .clk(Clock), .D(or_2_out), .Q(Start), .preset(1'b0), .reset(Clear));  // open: Qn
  Counter #(.width(8), .max('hff), .ongoal("wrap"), .trigger("rising"), .behavior("new")) counter_1 (
    .load(1'b0), .count(1'b1), .Q(counter_1_q), .clk(Clock_2), .clr(Clear), .preset(1'b0), .down(1'b0));  // open: D, carry

  assign Clear_2 = Clear;

  // Notes on the sheet:
  //   最高6位
endmodule

module \显示器  (
  input  [31:0] in_1,
  output [3:0] D0,
  output [3:0] D1,
  output [3:0] D2,
  output [3:0] D3,
  output [3:0] D4,
  output [3:0] D5,
  output [3:0] D6,
  output [3:0] D7,
  output [3:0] D8,
  output [3:0] D9
);

  wire [31:0] divider_1_out, divider_2_out, divider_3_out, divider_4_out, divider_5_out, divider_7_out,
       divider_8_out, divider_9_out, divider_10_out;
  wire [31:4] divider_1_rem, divider_2_rem, divider_3_rem, divider_4_rem, divider_5_rem, divider_6_rem,
       divider_7_rem, divider_8_rem, divider_9_rem, divider_10_rem;

  Divider #(.width(32)) divider_1 (
    .a(in_1), .b(32'ha), .out(divider_1_out), .upper({32{1'b0}}), .rem({divider_1_rem, D0}));
  Divider #(.width(32)) divider_2 (
    .a(divider_9_out), .b(32'ha), .out(divider_2_out), .upper({32{1'b0}}), .rem({divider_2_rem, D4}));
  Divider #(.width(32)) divider_3 (
    .a(divider_10_out), .b(32'ha), .out(divider_3_out), .upper({32{1'b0}}), .rem({divider_3_rem, D8}));
  Divider #(.width(32)) divider_4 (
    .a(divider_1_out), .b(32'ha), .out(divider_4_out), .upper({32{1'b0}}), .rem({divider_4_rem, D1}));
  Divider #(.width(32)) divider_5 (
    .a(divider_2_out), .b(32'ha), .out(divider_5_out), .upper({32{1'b0}}), .rem({divider_5_rem, D5}));
  Divider #(.width(32)) divider_6 (
    .a(divider_3_out), .b(32'ha), .upper({32{1'b0}}), .rem({divider_6_rem, D9}));  // open: out
  Divider #(.width(32)) divider_7 (
    .a(divider_4_out), .b(32'ha), .out(divider_7_out), .upper({32{1'b0}}), .rem({divider_7_rem, D2}));
  Divider #(.width(32)) divider_8 (
    .a(divider_5_out), .b(32'ha), .out(divider_8_out), .upper({32{1'b0}}), .rem({divider_8_rem, D6}));
  Divider #(.width(32)) divider_9 (
    .a(divider_7_out), .b(32'ha), .out(divider_9_out), .upper({32{1'b0}}), .rem({divider_9_rem, D3}));
  Divider #(.width(32)) divider_10 (
    .a(divider_8_out), .b(32'ha), .out(divider_10_out), .upper({32{1'b0}}), .rem({divider_10_rem, D7}));
endmodule

module \Fibonacci计算器  (
  input  [5:0] n,
  input  in_2,
  input  in_3,
  output [3:0] out_4,
  output [3:0] out_5,
  output [3:0] out_6,
  output [3:0] out_7,
  output [3:0] out_8,
  output [3:0] out_9,
  output [3:0] out_10,
  output [3:0] out_11,
  output [3:0] out_12,
  output [3:0] out_13
);

  wire \控制器_1_clear_2 , \控制器_1_clock_2 , \控制器_1_ni_1 , \控制器_1_start ;
  wire [31:0] \矩阵快速幂算法迭代_1_fi ;

  \控制器  \u_控制器_1  (
    .n(n), .Clock(in_3), .Clear(in_2), .Ni_1(\控制器_1_ni_1 ), .Start(\控制器_1_start ), .Clock_2(\控制器_1_clock_2 ),
    .Clear_2(\控制器_1_clear_2 ));
  \矩阵快速幂算法迭代  \u_矩阵快速幂算法迭代_1  (
    .Start(\控制器_1_start ), .Clock(\控制器_1_clock_2 ), .Clear(\控制器_1_clear_2 ), .Fi(\矩阵快速幂算法迭代_1_fi ),
    .Ni_1(\控制器_1_ni_1 ));
  \显示器  \u_显示器_1  (
    .in_1(\矩阵快速幂算法迭代_1_fi ), .D0(out_13), .D4(out_9), .D8(out_5), .D1(out_12), .D5(out_8), .D9(out_4),
    .D2(out_11), .D6(out_7), .D3(out_10), .D7(out_6));
endmodule

module \斐波那契_Fibonacci_数列计算器验证电路  (
  input  [5:0] in_1
);

  wire button_1_out, button_2_out;
  wire [3:0] \fibonacci计算器_1_out_4 , \fibonacci计算器_1_out_5 , \fibonacci计算器_1_out_6 , \fibonacci计算器_1_out_7 ,
       \fibonacci计算器_1_out_8 , \fibonacci计算器_1_out_9 , \fibonacci计算器_1_out_10 , \fibonacci计算器_1_out_11 ,
       \fibonacci计算器_1_out_12 , \fibonacci计算器_1_out_13 ;

  Button button_1 (.out(button_1_out));
  Button button_2 (.out(button_2_out));
  \Fibonacci计算器  \fibonacci计算器_1  (
    .n(in_1), .in_2(button_1_out), .in_3(button_2_out), .out_4(\fibonacci计算器_1_out_4 ),
    .out_5(\fibonacci计算器_1_out_5 ), .out_6(\fibonacci计算器_1_out_6 ), .out_7(\fibonacci计算器_1_out_7 ),
    .out_8(\fibonacci计算器_1_out_8 ), .out_9(\fibonacci计算器_1_out_9 ), .out_10(\fibonacci计算器_1_out_10 ),
    .out_11(\fibonacci计算器_1_out_11 ), .out_12(\fibonacci计算器_1_out_12 ), .out_13(\fibonacci计算器_1_out_13 ));
  Hex_Digit_Display hex_digit_display_1 (.value(\fibonacci计算器_1_out_4 ));  // open: dp
  Hex_Digit_Display hex_digit_display_2 (.value(\fibonacci计算器_1_out_5 ));  // open: dp
  Hex_Digit_Display hex_digit_display_3 (.value(\fibonacci计算器_1_out_6 ));  // open: dp
  Hex_Digit_Display hex_digit_display_4 (.value(\fibonacci计算器_1_out_7 ));  // open: dp
  Hex_Digit_Display hex_digit_display_5 (.value(\fibonacci计算器_1_out_8 ));  // open: dp
  Hex_Digit_Display hex_digit_display_6 (.value(\fibonacci计算器_1_out_9 ));  // open: dp
  Hex_Digit_Display hex_digit_display_7 (.value(\fibonacci计算器_1_out_10 ));  // open: dp
  Hex_Digit_Display hex_digit_display_8 (.value(\fibonacci计算器_1_out_11 ));  // open: dp
  Hex_Digit_Display hex_digit_display_9 (.value(\fibonacci计算器_1_out_12 ));  // open: dp
  Hex_Digit_Display hex_digit_display_10 (.value(\fibonacci计算器_1_out_13 ));  // open: dp
endmodule
